// Logisim project ulaAtualizada.circ as structural Verilog: 7 circuits, main circuit main
module main (
  input  [3:0] a,
  input  [3:0] b,
  input  [2:0] fs,
  output [3:0] \output ,
  output cout_sum,
  output cout_sub,
  output [3:0] sub,
  output [3:0] div,
  output [3:0] resto,
  output [3:0] mult
);

  wire decoder_1_codes0, decoder_1_codes1, decoder_1_codes2, decoder_1_codes4, soma_1_cout, soma_2_cout,
       soma_3_cout;
  wire [3:0] and_1_out, and_2_out, and_3_out, and_4_out, logunit_1_sa, logunit_1_sb, logunit_1_uits0,
       logunit_1_units1, logunit_1_units3, soma_1_sum;
  wire [3:3] decoder_1_codes3, decoder_1_codes5, decoder_1_codes6, decoder_1_codes7;

  decoder decoder_1 (
    .f2(fs[2]), .f1(fs[1]), .f0(fs[0]), .codeS0(decoder_1_codes0), .codeS1(decoder_1_codes1),
    .codeS2(decoder_1_codes2), .codeS3(decoder_1_codes3[3]), .codeS4(decoder_1_codes4),
    .codeS5(decoder_1_codes5[3]), .codeS6(decoder_1_codes6[3]), .codeS7(decoder_1_codes7[3]));
  logUnit logunit_1 (
    .a(a), .b(b), .SA(logunit_1_sa), .SB(logunit_1_sb), .inDecoder0(decoder_1_codes0),
    .inDecoder1(decoder_1_codes1), .inDecoder3(decoder_1_codes2), .uitS0(logunit_1_uits0),
    .unitS1(logunit_1_units1), .unitS3(logunit_1_units3));
  Multiplier #(.width(4)) multiplier_1 (.a(logunit_1_sa), .b(logunit_1_sb), .out(mult));  // open: cin, cout
  soma soma_1 (
    .a(logunit_1_sa[0]), .b(logunit_1_sb[0]), .e0(decoder_1_codes4), .cin(1'b0), .sum(soma_1_sum[0]),
    .cout(soma_1_cout));
  sub sub_1 (
    .e0(decoder_1_codes5[3]), .cout(cout_sub), .a3(logunit_1_sb[3]), .b3(logunit_1_sa[3]),
    .a2(logunit_1_sb[2]), .b2(logunit_1_sa[2]), .a1(logunit_1_sb[1]), .b1(logunit_1_sa[1]),
    .a0(logunit_1_sb[0]), .b0(logunit_1_sa[0]), .s3(sub[3]), .s2(sub[2]), .s1(sub[1]), .s0(sub[0]));
  Divider #(.width(4)) divider_1 (.a(logunit_1_sb), .b(logunit_1_sa), .out(div), .rem(resto));  // open: upper
  soma soma_2 (
    .a(logunit_1_sa[1]), .b(logunit_1_sb[1]), .e0(decoder_1_codes4), .cin(soma_1_cout), .sum(soma_1_sum[1]),
    .cout(soma_2_cout));
  soma soma_3 (
    .a(logunit_1_sa[2]), .b(logunit_1_sb[2]), .e0(decoder_1_codes4), .cin(soma_2_cout), .sum(soma_1_sum[2]),
    .cout(soma_3_cout));
  soma soma_4 (
    .a(logunit_1_sa[3]), .b(logunit_1_sb[3]), .e0(decoder_1_codes4), .cin(soma_3_cout), .sum(soma_1_sum[3]),
    .cout(cout_sum));
  assign and_1_out = {4{decoder_1_codes5[3]}} & sub;  // AND_Gate and_1, 4 bits wide
  assign and_2_out = resto & {4{decoder_1_codes3[3]}};  // AND_Gate and_2, 4 bits wide
  assign and_3_out = div & {4{decoder_1_codes6[3]}};  // AND_Gate and_3, 4 bits wide
  assign \output  = logunit_1_uits0 | logunit_1_units1 | logunit_1_units3 | soma_1_sum | and_1_out | and_3_out | and_2_out | and_4_out;  // OR_Gate or_1, 4 bits wide
  assign and_4_out = mult & {4{decoder_1_codes7[3]}};  // AND_Gate and_4, 4 bits wide

  // Notes on the sheet:
  //   000 = and
  //   001 = or
  //   010 = resto divisao
  //   011 = xor
  //   100 = adicao
  //   101 = subtracao
  //   110 = divisao
  //   111 = multiplicacao
endmodule

module decoder (
  input  f2,
  input  f1,
  input  f0,
  output codeS0,
  output codeS1,
  output codeS2,
  output codeS3,
  output codeS4,
  output codeS5,
  output codeS6,
  output codeS7
);

  wire not_1_out, not_2_out, not_3_out, not_4_out, not_5_out, not_6_out, not_7_out, not_8_out, not_9_out,
       not_10_out, not_11_out, not_12_out;

  not not_1 (not_1_out, f2);
  not not_2 (not_2_out, f2);
  not not_3 (not_3_out, f1);
  not not_4 (not_4_out, f0);
  not not_5 (not_5_out, f2);
  not not_6 (not_6_out, f1);
  not not_7 (not_7_out, f0);
  not not_8 (not_8_out, f2);
  not not_9 (not_9_out, f1);
  not not_10 (not_10_out, f0);
  not not_11 (not_11_out, f1);
  not not_12 (not_12_out, f0);
  and and_1 (codeS0, not_2_out, not_3_out, not_4_out);
  and and_2 (codeS1, not_5_out, not_6_out, f0);
  and and_3 (codeS2, not_1_out, f1, not_7_out);
  and and_4 (codeS3, not_8_out, f1, f0);
  and and_5 (codeS4, f2, not_9_out, not_10_out);
  and and_6 (codeS5, f2, not_11_out, f0);
  and and_7 (codeS6, f2, f1, not_12_out);
  and and_8 (codeS7, f2, f1, f0);
endmodule

module logUnit (
  input  [3:0] a,
  input  [3:0] b,
  input  inDecoder3,
  input  inDecoder0,
  input  inDecoder1,
  output [3:0] uitS0,
  output [3:0] unitS1,
  output [3:0] unitS3,
  output [3:0] SA,
  output [3:0] SB
);

  wire [3:0] and_1_out, or_1_out, xor_1_out;

  assign and_1_out = a & b;  // AND_Gate and_1, 4 bits wide
  assign or_1_out = a | b;  // OR_Gate or_1, 4 bits wide
  assign xor_1_out = a ^ b;  // XOR_Gate xor_1, 4 bits wide
  assign uitS0 = and_1_out & {4{inDecoder0}};  // AND_Gate and_2, 4 bits wide
  assign unitS1 = or_1_out & {4{inDecoder1}};  // AND_Gate and_3, 4 bits wide
  assign unitS3 = xor_1_out & {4{inDecoder3}};  // AND_Gate and_4, 4 bits wide

  assign SA = a;
  assign SB = b;
endmodule

module soma (
  input  cin,
  input  a,
  input  b,
  input  e0,
  output sum,
  output cout
);

  wire and_1_out, and_2_out, xor_1_out, xor_2_out;

  and and_1 (and_1_out, e0, b, a);
  xor xor_1 (xor_1_out, a, b);
  or or_1 (cout, and_1_out, and_2_out);
  and and_2 (and_2_out, e0, xor_1_out, cin);
  xor xor_2 (xor_2_out, cin, xor_1_out);
  and and_3 (sum, xor_2_out, e0);
endmodule

module sub (
  input  a3,
  input  b3,
  input  a2,
  input  b2,
  input  a1,
  input  b1,
  input  a0,
  input  b0,
  input  e0,
  output cout,
  output s3,
  output s2,
  output s1,
  output s0
);

  wire and_1_out, mux_1_s, mux_2_s, mux_3_s, mux_4_s, not_1_out, not_2_out, not_3_out, not_4_out,
       somador_2_cout, somador_3_cout, somador_4_cout;

  and and_1 (and_1_out, 1'b1, e0);
  not not_1 (not_1_out, b3);
  mux mux_1 (.minus_b(not_1_out), .b(b3), .c(and_1_out), .s(mux_1_s));
  somador somador_1 (.a(a3), .b(mux_1_s), .cin(somador_2_cout), .s(s3), .cout(cout));
  not not_2 (not_2_out, b2);
  mux mux_2 (.minus_b(not_2_out), .b(b2), .c(and_1_out), .s(mux_2_s));
  somador somador_2 (.a(a2), .b(mux_2_s), .cin(somador_3_cout), .s(s2), .cout(somador_2_cout));
  not not_3 (not_3_out, b1);
  mux mux_3 (.minus_b(not_3_out), .b(b1), .c(and_1_out), .s(mux_3_s));
  somador somador_3 (.a(a1), .b(mux_3_s), .cin(somador_4_cout), .s(s1), .cout(somador_3_cout));
  not not_4 (not_4_out, b0);
  mux mux_4 (.minus_b(not_4_out), .b(b0), .c(and_1_out), .s(mux_4_s));
  somador somador_4 (.a(a0), .b(mux_4_s), .cin(and_1_out), .s(s0), .cout(somador_4_cout));
endmodule

module mux (
  input  minus_b,
  input  b,
  input  c,
  output s
);

  wire and_1_out, and_2_out, not_1_out;

  and and_1 (and_1_out, minus_b, c);
  and and_2 (and_2_out, b, not_1_out);
  not not_1 (not_1_out, c);
  or or_1 (s, and_1_out, and_2_out);
endmodule

module somador (
  input  a,
  input  b,
  input  cin,
  output s,
  output cout
);

  wire and_1_out, and_2_out, and_3_out, xor_1_out;

  xor xor_1 (xor_1_out, b, cin);
  and and_1 (and_1_out, b, cin);
  and and_2 (and_2_out, a, b);
  and and_3 (and_3_out, a, cin);
  xor xor_2 (s, a, xor_1_out);
  or or_1 (cout, and_1_out, and_2_out, and_3_out);
endmodule
