// Logisim project n.circ as structural Verilog
module decoder (
  input  f2,
  input  f1,
  input  f0,
  output codeS0,
  output codeS1,
  output codeS2,
  output codeS3,
  output codeS4,
  output codeS5,
  output codeS6,
  output codeS7
);

  wire not_1_out, not_2_out, not_3_out, not_4_out, not_5_out, not_6_out, not_7_out, not_8_out, not_9_out,
       not_10_out, not_11_out, not_12_out;

  not not_1 (not_1_out, f2);
  not not_2 (not_2_out, f2);
  not not_3 (not_3_out, f1);
  not not_4 (not_4_out, f0);
  not not_5 (not_5_out, f2);
  not not_6 (not_6_out, f1);
  not not_7 (not_7_out, f0);
  not not_8 (not_8_out, f2);
  not not_9 (not_9_out, f1);
  not not_10 (not_10_out, f0);
  not not_11 (not_11_out, f1);
  not not_12 (not_12_out, f0);
  and and_1 (codeS0, not_2_out, not_3_out, not_4_out);
  and and_2 (codeS1, not_5_out, not_6_out, f0);
  and and_3 (codeS2, not_1_out, f1, not_7_out);
  and and_4 (codeS3, not_8_out, f1, f0);
  and and_5 (codeS4, f2, not_9_out, not_10_out);
  and and_6 (codeS5, f2, not_11_out, f0);
  and and_7 (codeS6, f2, f1, not_12_out);
  and and_8 (codeS7, f2, f1, f0);
endmodule

module logUnit (
  input  e0,
  input  e1,
  input  inDecoder0,
  input  inDecoder1,
  input  inDecoder2,
  output uitS0,
  output unitS1,
  output unitS2,
  output Se0,
  output Se1
);

  wire and_1_out, not_1_out, or_1_out;

  and and_1 (and_1_out, e0, e1);
  or or_1 (or_1_out, e0, e1);
  not not_1 (not_1_out, e1);
  and and_2 (uitS0, and_1_out, inDecoder0);
  and and_3 (unitS1, or_1_out, inDecoder1);
  and and_4 (unitS2, not_1_out, inDecoder2);

  assign Se0 = e0;
  assign Se1 = e1;
endmodule

module adder (
  input  cin,
  input  e0,
  input  e1,
  input  e2,
  output sum,
  output cout
);

  wire and_1_out, and_2_out, xor_1_out, xor_2_out;

  and and_1 (and_1_out, e2, e1, e0);
  xor xor_1 (xor_1_out, e0, e1);
  or or_1 (cout, and_1_out, and_2_out);
  and and_2 (and_2_out, e2, xor_1_out, cin);
  xor xor_2 (xor_2_out, cin, xor_1_out);
  and and_3 (sum, xor_2_out, e2);
endmodule

module ula (
  input  in_1,
  input  in_2,
  input  in_3,
  input  in_4,
  input  in_5,
  input  in_6,
  input  in_7,
  input  in_8,
  input  in_9,
  output out_10,
  output out_11
);

  wire adder_1_p6, and_1_out, and_2_out, decoder_1_codes0, decoder_1_codes1, decoder_1_codes2,
       decoder_1_codes3, decoder_1_codes4, logunit_1_p8, logunit_1_p9, logunit_1_p10, xor_1_out;
  wire [3:0] divider_1_out, divider_1_rem, logunit_1_p3, logunit_1_p4, sub_1_p13;

  and and_1 (and_1_out, in_3, in_4);
  and and_2 (and_2_out, in_5, in_6);
  xor xor_1 (xor_1_out, in_2, and_1_out);
  decoder decoder_1 (
    .f2(in_7), .f1(in_8), .f0(in_9), .codeS0(decoder_1_codes0), .codeS1(decoder_1_codes1),
    .codeS2(decoder_1_codes2), .codeS3(decoder_1_codes3), .codeS4(decoder_1_codes4));  // open: codeS5, codeS6, codeS7
  // logUnit logunit_1: pin names not known; wires that end beside it: xor_1_out, and_2_out, logunit_1_p3, logunit_1_p4, decoder_1_codes0, decoder_1_codes1, decoder_1_codes2, logunit_1_p8, logunit_1_p9, logunit_1_p10
  // adder adder_1: pin names not known; wires that end beside it: logunit_1_p4, logunit_1_p3, decoder_1_codes3, in_1, out_11, adder_1_p6
  or or_1 (out_10, logunit_1_p8, logunit_1_p9, logunit_1_p10, adder_1_p6);
  // sub sub_1: pin names not known; wires that end beside it: decoder_1_codes4, logunit_1_p3[3], logunit_1_p4[3], logunit_1_p3[2], logunit_1_p4[2], logunit_1_p3[1], logunit_1_p4[1], logunit_1_p3[0], logunit_1_p4[0], sub_1_p13[3], sub_1_p13[2], sub_1_p13[1], sub_1_p13[0]
  Divider #(.width(4)) divider_1 (.a(sub_1_p13), .b(4'b1010), .out(divider_1_out), .rem(divider_1_rem));  // open: upper
  Hex_Digit_Display hex_digit_display_1 (.value(divider_1_out));  // open: dp
  Hex_Digit_Display hex_digit_display_2 (.value(divider_1_rem));  // open: dp
endmodule

module sub (
  input  c0,
  input  a3,
  input  b3,
  input  a2,
  input  b2,
  input  a1,
  input  b1,
  input  a0,
  input  b0,
  input  a7,
  input  b7,
  input  a6,
  input  b6,
  input  a5,
  input  b5,
  input  a4,
  input  b4,
  output s3,
  output s2,
  output s1,
  output s0,
  output cout,
  output s,
  output s_2,
  output s_3,
  output s_4
);

  wire mux_1_s, mux_2_s, mux_3_s, mux_4_s, mux_5_s, mux_6_s, mux_7_s, mux_8_s, not_1_out, not_2_out,
       not_3_out, not_4_out, not_5_out, not_6_out, not_7_out, not_8_out, somador_1_cout, somador_3_cout,
       somador_4_cout, somador_5_cout, somador_6_cout, somador_7_cout, somador_8_cout;

  not not_1 (not_1_out, b3);
  mux mux_1 (.minus_b(not_1_out), .b(b3), .c(c0), .s(mux_1_s));
  somador somador_1 (.a(a3), .b(mux_1_s), .cin(somador_3_cout), .s(s3), .cout(somador_1_cout));
  not not_2 (not_2_out, b7);
  mux mux_2 (.minus_b(not_2_out), .b(b7), .c(c0), .s(mux_2_s));
  somador somador_2 (.a(a7), .b(mux_2_s), .cin(somador_4_cout), .s(s), .cout(cout));
  not not_3 (not_3_out, b2);
  mux mux_3 (.minus_b(not_3_out), .b(b2), .c(c0), .s(mux_3_s));
  not not_4 (not_4_out, b6);
  mux mux_4 (.minus_b(not_4_out), .b(b6), .c(c0), .s(mux_4_s));
  somador somador_3 (.a(a2), .b(mux_3_s), .cin(somador_5_cout), .s(s2), .cout(somador_3_cout));
  somador somador_4 (.a(a6), .b(mux_4_s), .cin(somador_6_cout), .s(s_2), .cout(somador_4_cout));
  not not_5 (not_5_out, b1);
  mux mux_5 (.minus_b(not_5_out), .b(b1), .c(c0), .s(mux_5_s));
  somador somador_5 (.a(a1), .b(mux_5_s), .cin(somador_7_cout), .s(s1), .cout(somador_5_cout));
  not not_6 (not_6_out, b5);
  mux mux_6 (.minus_b(not_6_out), .b(b5), .c(c0), .s(mux_6_s));
  somador somador_6 (.a(a5), .b(mux_6_s), .cin(somador_8_cout), .s(s_3), .cout(somador_6_cout));
  not not_7 (not_7_out, b0);
  mux mux_7 (.minus_b(not_7_out), .b(b0), .c(c0), .s(mux_7_s));
  somador somador_7 (.a(a0), .b(mux_7_s), .cin(c0), .s(s0), .cout(somador_7_cout));
  not not_8 (not_8_out, b4);
  mux mux_8 (.minus_b(not_8_out), .b(b4), .c(c0), .s(mux_8_s));
  somador somador_8 (.a(a4), .b(mux_8_s), .cin(somador_1_cout), .s(s_4), .cout(somador_8_cout));
endmodule

module mux (
  input  minus_b,
  input  b,
  input  c,
  output s
);

  wire and_1_out, and_2_out, not_1_out;

  and and_1 (and_1_out, minus_b, c);
  and and_2 (and_2_out, b, not_1_out);
  not not_1 (not_1_out, c);
  or or_1 (s, and_1_out, and_2_out);
endmodule

module somador (
  input  a,
  input  b,
  input  cin,
  output s,
  output cout
);

  wire and_1_out, and_2_out, and_3_out, xor_1_out;

  xor xor_1 (xor_1_out, b, cin);
  and and_1 (and_1_out, b, cin);
  and and_2 (and_2_out, a, b);
  and and_3 (and_3_out, a, cin);
  xor xor_2 (s, a, xor_1_out);
  or or_1 (cout, and_1_out, and_2_out, and_3_out);
endmodule
