// Logisim project sequencias.circ as structural Verilog: 11 circuits, main circuit main
module main (
);

  wire and_1_out, and_2_out, clock_1_out, clock_2_out, clock_3_out, or_1_out, or_2_out, q0_2_qn, q1_2_qn,
       q2_2_qn;
  wire [2:0] q0_q;
  wire [3:0] j_k_ff_4_q, q0_2_q;

  Clock clock_1 (.out(clock_1_out));
  and and_1 (and_1_out, q2_2_qn, q1_2_qn);
  Clock clock_2 (.out(clock_2_out));
  J_K_Flip_Flop q3 (.J(and_1_out), .clk(clock_1_out), .K(q0_2_q[2]), .Q(q0_2_q[3]));  // open: Qn, preset, en, reset
  J_K_Flip_Flop q2 (.J(q0_q[0]), .clk(clock_2_out), .K(q0_q[0]), .Q(q0_q[2]));  // open: Qn, preset, en, reset
  or or_1 (or_1_out, q0_2_q[3], q0_2_qn);
  or or_2 (or_2_out, q0_2_q[3], q0_2_q[1]);
  Hex_Digit_Display hex_digit_display_1 (.value(q0_2_q));  // open: dp
  J_K_Flip_Flop q1 (.J(1'b1), .clk(clock_2_out), .K(1'b1), .Q(q0_q[1]));  // open: Qn, preset, en, reset
  Hex_Digit_Display hex_digit_display_2 (.value({1'b0, q0_q}));  // open: dp
  J_K_Flip_Flop q2_2 (
    .J(or_1_out), .clk(clock_1_out), .K(or_2_out), .Q(q0_2_q[2]), .Qn(q2_2_qn));  // open: preset, en, reset
  J_K_Flip_Flop q0 (.J(1'b1), .clk(clock_2_out), .K(1'b1), .Q(q0_q[0]));  // open: Qn, preset, en, reset
  J_K_Flip_Flop q1_2 (
    .J(1'b1), .clk(clock_1_out), .K(q2_2_qn), .Q(q0_2_q[1]), .Qn(q1_2_qn));  // open: preset, en, reset
  and and_2 (and_2_out, q0_2_q[3], q1_2_qn);
  J_K_Flip_Flop q0_2 (
    .J(1'b1), .clk(clock_1_out), .K(and_2_out), .Q(q0_2_q[0]), .Qn(q0_2_qn));  // open: preset, en, reset
  Clock clock_3 (.out(clock_3_out));
  J_K_Flip_Flop j_k_ff_1 (
    .J(j_k_ff_4_q[2]), .clk(clock_3_out), .K(1'b1), .Q(j_k_ff_4_q[3]));  // open: Qn, preset, en, reset
  Hex_Digit_Display hex_digit_display_3 (.value(j_k_ff_4_q));  // open: dp
  J_K_Flip_Flop j_k_ff_2 (
    .J(j_k_ff_4_q[1]), .clk(clock_3_out), .K(1'b1), .Q(j_k_ff_4_q[2]));  // open: Qn, preset, en, reset
  J_K_Flip_Flop j_k_ff_3 (
    .J(j_k_ff_4_q[0]), .clk(clock_3_out), .K(1'b1), .Q(j_k_ff_4_q[1]));  // open: Qn, preset, en, reset
  J_K_Flip_Flop j_k_ff_4 (
    .J(j_k_ff_4_q[3]), .clk(clock_3_out), .K(1'b1), .Q(j_k_ff_4_q[0]));  // open: Qn, preset, en, reset
endmodule

module segundosU (
);

  wire and_1_out, and_2_out, and_3_out, and_4_out, clock_1_out, not_1_out, not_2_out, not_3_out, or_1_out;
  wire [3:0] q0_q;

  and and_1 (and_1_out, q0_q[0], q0_q[1], q0_q[2]);
  Clock clock_1 (.out(clock_1_out));
  and and_2 (and_2_out, q0_q[0], q0_q[1]);
  J_K_Flip_Flop q3 (.J(and_1_out), .clk(clock_1_out), .K(q0_q[0]), .Q(q0_q[3]));  // open: Qn, preset, en, reset
  not not_1 (not_1_out, q0_q[2]);
  J_K_Flip_Flop q2 (.J(and_2_out), .clk(clock_1_out), .K(1'b0), .Q(q0_q[2]));  // open: Qn, preset, en, reset
  and and_3 (and_3_out, not_1_out, q0_q[0], not_2_out);
  not not_2 (not_2_out, q0_q[3]);
  and and_4 (and_4_out, q0_q[0], not_2_out);
  Hex_Digit_Display hex_digit_display_1 (.value(q0_q));  // open: dp
  J_K_Flip_Flop q1 (.J(and_4_out), .clk(clock_1_out), .K(and_3_out), .Q(q0_q[1]));  // open: Qn, preset, en, reset
  or or_1 (or_1_out, not_3_out, and_3_out);
  not not_3 (not_3_out, q0_q[1]);
  J_K_Flip_Flop q0 (.J(1'b1), .clk(clock_1_out), .K(or_1_out), .Q(q0_q[0]));  // open: Qn, preset, en, reset
endmodule

module segundosUautomatico (
  input  q0,
  input  q1,
  input  q2,
  input  q3,
  output q0_2,
  output q1_2,
  output q2_2,
  output q3_2
);

  wire and_1_out, and_2_out, and_3_out, and_4_out, and_5_out, and_6_out, and_7_out, not_1_out, not_2_out,
       not_3_out, not_4_out, not_5_out, not_6_out, not_7_out;

  not not_1 (not_1_out, q3);
  not not_2 (not_2_out, q1);
  not not_3 (not_3_out, q2);
  not not_4 (not_4_out, q3);
  not not_5 (not_5_out, q0);
  not not_6 (not_6_out, q2);
  not not_7 (not_7_out, q3);
  not not_8 (q3_2, q3);
  and and_1 (and_1_out, q1, q2, q3);
  and and_2 (and_2_out, q0, not_1_out);
  and and_3 (and_3_out, not_2_out, q2, q3);
  and and_4 (and_4_out, q1, not_3_out);
  and and_5 (and_5_out, q1, not_4_out);
  and and_6 (and_6_out, not_5_out, not_6_out, q3);
  and and_7 (and_7_out, q2, not_7_out);
  or or_1 (q0_2, and_1_out, and_2_out);
  or or_2 (q1_2, and_3_out, and_4_out, and_5_out);
  or or_3 (q2_2, and_6_out, and_7_out);
  Hex_Digit_Display hex_digit_display_1 (.value({q3_2, q2_2, q1_2, q0_2}));  // open: dp
endmodule

module segundosU7saidas (
  input  q0,
  input  q1,
  input  q2,
  input  q3,
  output q0_2,
  output q1_2,
  output q2_2,
  output q3_2,
  output a4,
  output a5,
  output a6
);

  wire and_1_out, and_2_out, and_3_out, and_4_out, and_5_out, and_6_out, and_7_out, and_8_out, and_9_out,
       and_10_out, and_11_out, and_12_out, and_13_out, and_14_out, and_15_out, and_16_out, and_17_out,
       and_18_out, and_19_out, and_20_out, and_21_out, and_22_out, and_23_out, and_24_out, and_25_out,
       and_26_out, not_1_out, not_2_out, not_3_out, not_4_out, not_5_out, not_6_out, not_7_out, not_8_out,
       not_9_out, not_10_out, not_11_out, not_12_out, not_13_out, not_14_out, not_15_out, not_16_out,
       not_17_out, not_18_out, not_19_out, not_20_out, not_21_out, not_22_out, not_23_out, not_24_out,
       not_25_out, not_26_out, not_27_out, not_28_out, not_29_out, not_30_out, not_31_out, not_32_out,
       not_33_out, not_34_out, not_35_out, not_36_out, not_37_out, not_38_out, not_39_out, not_40_out,
       not_41_out, not_42_out, not_43_out, not_44_out, not_45_out, not_46_out, not_47_out, not_48_out,
       not_49_out, not_50_out, not_51_out, not_52_out;

  not not_1 (not_1_out, q0);
  not not_2 (not_2_out, q1);
  and and_1 (and_1_out, not_1_out, not_2_out, not_3_out);
  not not_3 (not_3_out, q3);
  not not_4 (not_4_out, q0);
  and and_2 (and_2_out, not_4_out, q2);
  not not_5 (not_5_out, q0);
  and and_3 (and_3_out, not_5_out, q1, q3);
  not not_6 (not_6_out, q1);
  and and_4 (and_4_out, q0, not_6_out, not_7_out);
  not not_7 (not_7_out, q2);
  not not_8 (not_8_out, q0);
  and and_5 (and_5_out, not_8_out, not_9_out);
  not not_9 (not_9_out, q1);
  not not_10 (not_10_out, q0);
  not not_11 (not_11_out, q2);
  and and_6 (and_6_out, not_10_out, not_11_out, not_12_out);
  not not_12 (not_12_out, q3);
  not not_13 (not_13_out, q1);
  and and_7 (and_7_out, not_13_out, not_14_out);
  not not_14 (not_14_out, q2);
  not not_15 (not_15_out, q0);
  and and_8 (and_8_out, not_15_out, q2, q3);
  not not_16 (not_16_out, q1);
  and and_9 (and_9_out, not_16_out, not_17_out);
  not not_17 (not_17_out, q2);
  not not_18 (not_18_out, q0);
  and and_10 (and_10_out, not_18_out, q3);
  not not_19 (not_19_out, q0);
  and and_11 (and_11_out, not_19_out, q1);
  not not_20 (not_20_out, q0);
  not not_21 (not_21_out, q1);
  not not_22 (not_22_out, q3);
  not not_23 (not_23_out, q0);
  not not_24 (not_24_out, q1);
  not not_25 (not_25_out, q0);
  not not_26 (not_26_out, q3);
  not not_27 (not_27_out, q0);
  not not_28 (not_28_out, q2);
  not not_29 (not_29_out, q1);
  not not_30 (not_30_out, q2);
  not not_31 (not_31_out, q1);
  not not_32 (not_32_out, q2);
  and and_12 (and_12_out, not_31_out, not_32_out, not_33_out);
  not not_33 (not_33_out, q3);
  not not_34 (not_34_out, q0);
  and and_13 (and_13_out, not_34_out, q2, not_35_out);
  not not_35 (not_35_out, q3);
  not not_36 (not_36_out, q0);
  not not_37 (not_37_out, q2);
  and and_14 (and_14_out, not_36_out, not_37_out, not_38_out);
  not not_38 (not_38_out, q3);
  not not_39 (not_39_out, q0);
  and and_15 (and_15_out, not_39_out, q1, not_40_out);
  not not_40 (not_40_out, q2);
  not not_41 (not_41_out, q0);
  and and_16 (and_16_out, not_41_out, q1, not_42_out);
  not not_42 (not_42_out, q3);
  not not_43 (not_43_out, q1);
  and and_17 (and_17_out, q0, not_43_out, not_44_out);
  not not_44 (not_44_out, q2);
  not not_45 (not_45_out, q0);
  not not_46 (not_46_out, q1);
  and and_18 (and_18_out, not_45_out, not_46_out, q2);
  not not_47 (not_47_out, q0);
  and and_19 (and_19_out, not_47_out, q1, not_48_out);
  not not_48 (not_48_out, q2);
  not not_49 (not_49_out, q0);
  and and_20 (and_20_out, not_49_out, q1, not_50_out);
  not not_50 (not_50_out, q3);
  not not_51 (not_51_out, q1);
  and and_21 (and_21_out, q0, not_51_out, not_52_out);
  not not_52 (not_52_out, q2);
  or or_1 (q0_2, and_1_out, and_2_out, and_3_out, and_4_out);
  or or_2 (q1_2, and_5_out, and_6_out, and_7_out, and_8_out);
  or or_3 (q2_2, and_9_out, and_10_out, and_11_out);
  and and_22 (and_22_out, not_20_out, not_21_out, not_22_out);
  and and_23 (and_23_out, not_23_out, not_24_out, q2);
  and and_24 (and_24_out, not_25_out, q2, not_26_out);
  and and_25 (and_25_out, not_27_out, q1, not_28_out, q3);
  and and_26 (and_26_out, q0, not_29_out, not_30_out);
  or or_4 (a4, and_12_out, and_13_out);
  or or_5 (a5, and_14_out, and_15_out, and_16_out, and_17_out);
  or or_6 (a6, and_18_out, and_19_out, and_20_out, and_21_out);
  or or_7 (q3_2, and_22_out, and_23_out, and_24_out, and_25_out, and_26_out);
  _7_Segment_Display u_7_segment_display_1 (
    .g(a6), .f(a5), .a(q0_2), .b(q1_2), .e(a4), .d(q3_2), .c(q2_2));  // open: dp
endmodule

module segundosD (
);

  wire and_1_out, clock_1_out;
  wire [2:0] q2_q;

  and and_1 (and_1_out, ~q2_q[0], q2_q[1], q2_q[2]);  // AND_Gate
  Clock clock_1 (.out(clock_1_out));
  J_K_Flip_Flop #(.trigger("falling")) q2 (
    .J(1'b1), .clk(clock_1_out), .K(1'b1), .Q(q2_q[0]), .reset(and_1_out));  // open: Qn, preset, en
  Hex_Digit_Display hex_digit_display_1 (.value({1'b0, q2_q}));  // open: dp
  J_K_Flip_Flop #(.trigger("falling")) q1 (
    .J(1'b1), .clk(q2_q[0]), .K(1'b1), .Q(q2_q[1]), .reset(and_1_out));  // open: Qn, preset, en
  J_K_Flip_Flop #(.trigger("falling")) q0 (
    .J(1'b1), .clk(q2_q[1]), .K(1'b1), .Q(q2_q[2]), .reset(and_1_out));  // open: Qn, preset, en
endmodule

module _0a9 (
);

  wire and_1_out, clock_1_out;
  wire [3:0] q3_q;

  Clock clock_1 (.out(clock_1_out));
  J_K_Flip_Flop #(.trigger("falling")) q3 (
    .J(1'b1), .clk(clock_1_out), .K(1'b1), .Q(q3_q[0]), .reset(and_1_out));  // open: Qn, preset, en
  and and_1 (and_1_out, q3_q[3], ~q3_q[2], q3_q[1], ~q3_q[0]);  // AND_Gate
  J_K_Flip_Flop #(.trigger("falling")) q2 (
    .J(1'b1), .clk(q3_q[0]), .K(1'b1), .Q(q3_q[1]), .reset(and_1_out));  // open: Qn, preset, en
  J_K_Flip_Flop #(.trigger("falling")) q1 (
    .J(1'b1), .clk(q3_q[1]), .K(1'b1), .Q(q3_q[2]), .reset(and_1_out));  // open: Qn, preset, en
  J_K_Flip_Flop #(.trigger("falling")) q0 (
    .J(1'b1), .clk(q3_q[2]), .K(1'b1), .Q(q3_q[3]), .reset(and_1_out));  // open: Qn, preset, en
  Hex_Digit_Display hex_digit_display_1 (.value(q3_q));  // open: dp
endmodule

module _0a3 (
);

  wire clock_1_out;
  wire [1:0] q1_q;

  Clock clock_1 (.out(clock_1_out));
  Hex_Digit_Display hex_digit_display_1 (.value({2'b00, q1_q}));  // open: dp
  J_K_Flip_Flop #(.trigger("falling")) q1 (
    .J(1'b1), .clk(clock_1_out), .K(1'b1), .Q(q1_q[0]));  // open: Qn, preset, en, reset
  J_K_Flip_Flop #(.trigger("falling")) q0 (
    .J(1'b1), .clk(q1_q[0]), .K(1'b1), .Q(q1_q[1]));  // open: Qn, preset, en, reset
endmodule

module _0a2 (
);

  wire and_1_out, clock_1_out;
  wire [1:0] q1_q;

  and and_1 (and_1_out, q1_q[0], q1_q[1]);
  Clock clock_1 (.out(clock_1_out));
  Hex_Digit_Display hex_digit_display_1 (.value({2'b00, q1_q}));  // open: dp
  J_K_Flip_Flop #(.trigger("falling")) q1 (
    .J(1'b1), .clk(clock_1_out), .K(1'b1), .Q(q1_q[0]), .reset(and_1_out));  // open: Qn, preset, en
  J_K_Flip_Flop #(.trigger("falling")) q0 (
    .J(1'b1), .clk(q1_q[0]), .K(1'b1), .Q(q1_q[1]), .reset(and_1_out));  // open: Qn, preset, en
endmodule

module _0a59 (
  output out_1,
  output out_2,
  output out_3,
  output out_4,
  output out_5,
  output out_6,
  output out_7,
  output out_8,
  output out_9,
  output out_10,
  output out_11,
  output out_12,
  output out_13,
  output out_14
);

  wire and_1_out, and_2_out, and_3_out, clock_1_out, div2_1_s4, div2_1_s9, q0_q, q1_q, q2_q, q3_q, q4_q;
  wire [3:0] div1_1_s0, div1_1_s7, div1_2_s0, div1_2_s7, div2_1_s0, div2_1_s5;

  and and_1 (and_1_out, ~out_7, out_6, out_5, out_4, out_3, ~out_2, ~out_1);  // AND_Gate
  J_K_Flip_Flop #(.trigger("falling")) q6 (
    .J(1'b1), .clk(and_3_out), .K(1'b1), .Q(out_1), .reset(and_1_out));  // open: Qn, preset, en
  and and_2 (and_2_out, q0_q, q1_q, ~q2_q, ~q3_q, ~q4_q);  // AND_Gate
  J_K_Flip_Flop #(.trigger("falling")) q5 (
    .J(1'b1), .clk(out_1), .K(1'b1), .Q(out_2), .reset(and_1_out));  // open: Qn, preset, en
  J_K_Flip_Flop #(.trigger("falling")) q4 (
    .J(1'b1), .clk(and_1_out), .K(1'b1), .Q(q4_q), .reset(and_2_out));  // open: Qn, preset, en
  J_K_Flip_Flop #(.trigger("falling")) q3 (
    .J(1'b1), .clk(q4_q), .K(1'b1), .Q(q3_q), .reset(and_2_out));  // open: Qn, preset, en
  J_K_Flip_Flop #(.trigger("falling")) q4_2 (
    .J(1'b1), .clk(out_2), .K(1'b1), .Q(out_3), .reset(and_1_out));  // open: Qn, preset, en
  div1 div1_1 (
    .a6(out_7), .a5(out_6), .a4(out_5), .a3(out_4), .a2(out_3), .a1(out_2), .a0(out_1), .s10(div1_1_s7[3]),
    .s9(div1_1_s7[2]), .s8(div1_1_s7[1]), .s7(div1_1_s7[0]), .s3(div1_1_s0[3]), .s2(div1_1_s0[2]),
    .s1(div1_1_s0[1]), .s0(div1_1_s0[0]));  // open: s13, s12, s11, s6, s5, s4
  J_K_Flip_Flop #(.trigger("falling")) q2 (
    .J(1'b1), .clk(q3_q), .K(1'b1), .Q(q2_q), .reset(and_2_out));  // open: Qn, preset, en
  J_K_Flip_Flop #(.trigger("falling")) q3_2 (
    .J(1'b1), .clk(out_3), .K(1'b1), .Q(out_4), .reset(and_1_out));  // open: Qn, preset, en
  J_K_Flip_Flop #(.trigger("falling")) q2_2 (
    .J(1'b1), .clk(out_4), .K(1'b1), .Q(out_5), .reset(and_1_out));  // open: Qn, preset, en
  J_K_Flip_Flop #(.trigger("falling")) q1 (
    .J(1'b1), .clk(q2_q), .K(1'b1), .Q(q1_q), .reset(and_2_out));  // open: Qn, preset, en
  div2 div2_1 (
    .a4(q0_q), .a3(q1_q), .a2(q2_q), .a1(q3_q), .a0(q4_q), .s9(div2_1_s9), .s8(div2_1_s5[3]),
    .s7(div2_1_s5[2]), .s6(div2_1_s5[1]), .s5(div2_1_s5[0]), .s4(div2_1_s4), .s3(div2_1_s0[3]),
    .s2(div2_1_s0[2]), .s1(div2_1_s0[1]), .s0(div2_1_s0[0]));
  J_K_Flip_Flop #(.trigger("falling")) q0 (
    .J(1'b1), .clk(q1_q), .K(1'b1), .Q(q0_q), .reset(and_2_out));  // open: Qn, preset, en
  J_K_Flip_Flop #(.trigger("falling")) q1_2 (
    .J(1'b1), .clk(out_5), .K(1'b1), .Q(out_6), .reset(and_1_out));  // open: Qn, preset, en
  J_K_Flip_Flop #(.trigger("falling")) q0_2 (
    .J(1'b1), .clk(out_6), .K(1'b1), .Q(out_7), .reset(and_1_out));  // open: Qn, preset, en
  Hex_Digit_Display hex_digit_display_1 (.value(div2_1_s5));  // open: dp
  Clock clock_1 (.out(clock_1_out));
  and and_3 (and_3_out, ~out_14, out_13, out_12, out_11, out_10, ~out_9, ~out_8);  // AND_Gate
  Hex_Digit_Display hex_digit_display_2 (.value(div2_1_s0));  // open: dp
  J_K_Flip_Flop #(.trigger("falling")) q6_2 (
    .J(1'b1), .clk(clock_1_out), .K(1'b1), .Q(out_8), .reset(and_3_out));  // open: Qn, preset, en
  Hex_Digit_Display hex_digit_display_3 (.value(div1_1_s0));  // open: dp
  Hex_Digit_Display hex_digit_display_4 (.value(div1_1_s7));  // open: dp
  J_K_Flip_Flop #(.trigger("falling")) q5_2 (
    .J(1'b1), .clk(out_8), .K(1'b1), .Q(out_9), .reset(and_3_out));  // open: Qn, preset, en
  Hex_Digit_Display hex_digit_display_5 (.value(div1_2_s7));  // open: dp
  Hex_Digit_Display hex_digit_display_6 (.value(div1_2_s0));  // open: dp
  J_K_Flip_Flop #(.trigger("falling")) q4_3 (
    .J(1'b1), .clk(out_9), .K(1'b1), .Q(out_10), .reset(and_3_out));  // open: Qn, preset, en
  J_K_Flip_Flop #(.trigger("falling")) q3_3 (
    .J(1'b1), .clk(out_10), .K(1'b1), .Q(out_11), .reset(and_3_out));  // open: Qn, preset, en
  div1 div1_2 (
    .a6(out_14), .a5(out_13), .a4(out_12), .a3(out_11), .a2(out_10), .a1(out_9), .a0(out_8),
    .s10(div1_2_s7[3]), .s9(div1_2_s7[2]), .s8(div1_2_s7[1]), .s7(div1_2_s7[0]), .s3(div1_2_s0[3]),
    .s2(div1_2_s0[2]), .s1(div1_2_s0[1]), .s0(div1_2_s0[0]));  // open: s13, s12, s11, s6, s5, s4
  J_K_Flip_Flop #(.trigger("falling")) q2_3 (
    .J(1'b1), .clk(out_11), .K(1'b1), .Q(out_12), .reset(and_3_out));  // open: Qn, preset, en
  J_K_Flip_Flop #(.trigger("falling")) q1_3 (
    .J(1'b1), .clk(out_12), .K(1'b1), .Q(out_13), .reset(and_3_out));  // open: Qn, preset, en
  J_K_Flip_Flop #(.trigger("falling")) q0_3 (
    .J(1'b1), .clk(out_13), .K(1'b1), .Q(out_14), .reset(and_3_out));  // open: Qn, preset, en
endmodule

module div1 (
  input  a6,
  input  a5,
  input  a4,
  input  a3,
  input  a2,
  input  a1,
  input  a0,
  output s13,
  output s12,
  output s11,
  output s10,
  output s9,
  output s8,
  output s7,
  output s6,
  output s5,
  output s4,
  output s3,
  output s2,
  output s1,
  output s0
);

  Divider #(.width(7)) divider_1 (
    .a({a6, a5, a4, a3, a2, a1, a0}), .b(7'b0001010), .out({s13, s12, s11, s10, s9, s8, s7}),
    .rem({s6, s5, s4, s3, s2, s1, s0}));  // open: upper
endmodule

module div2 (
  input  a4,
  input  a3,
  input  a2,
  input  a1,
  input  a0,
  output s9,
  output s8,
  output s7,
  output s6,
  output s5,
  output s4,
  output s3,
  output s2,
  output s1,
  output s0
);

  Divider #(.width(5)) divider_1 (
    .a({a4, a3, a2, a1, a0}), .b(5'b01010), .out({s9, s8, s7, s6, s5}), .rem({s4, s3, s2, s1, s0}));  // open: upper
endmodule
