// Logisim project relogio.circ as structural Verilog: 3 circuits, main circuit 0a59
module _0a59 (
  output out_1,
  output out_2,
  output out_3,
  output out_4,
  output out_5,
  output out_6,
  output out_7,
  output out_8,
  output out_9,
  output out_10,
  output out_11,
  output out_12,
  output out_13,
  output out_14
);

  wire and_1_out, and_2_out, and_3_out, clock_1_out, div2_1_s4, div2_1_s9, q0_q, q1_q, q2_q, q3_q, q4_q;
  wire [3:0] div1_1_s0, div1_1_s7, div1_2_s0, div1_2_s7, div2_1_s0, div2_1_s5;

  and and_1 (and_1_out, ~out_7, out_6, out_5, out_4, out_3, ~out_2, ~out_1);  // AND_Gate
  J_K_Flip_Flop #(.trigger("falling")) q6 (
    .J(1'b1), .clk(and_3_out), .K(1'b1), .Q(out_1), .reset(and_1_out));  // open: Qn, preset, en
  and and_2 (and_2_out, q0_q, q1_q, ~q2_q, ~q3_q, ~q4_q);  // AND_Gate
  J_K_Flip_Flop #(.trigger("falling")) q5 (
    .J(1'b1), .clk(out_1), .K(1'b1), .Q(out_2), .reset(and_1_out));  // open: Qn, preset, en
  J_K_Flip_Flop #(.trigger("falling")) q4 (
    .J(1'b1), .clk(and_1_out), .K(1'b1), .Q(q4_q), .reset(and_2_out));  // open: Qn, preset, en
  J_K_Flip_Flop #(.trigger("falling")) q3 (
    .J(1'b1), .clk(q4_q), .K(1'b1), .Q(q3_q), .reset(and_2_out));  // open: Qn, preset, en
  J_K_Flip_Flop #(.trigger("falling")) q4_2 (
    .J(1'b1), .clk(out_2), .K(1'b1), .Q(out_3), .reset(and_1_out));  // open: Qn, preset, en
  div1 div1_1 (
    .a6(out_7), .a5(out_6), .a4(out_5), .a3(out_4), .a2(out_3), .a1(out_2), .a0(out_1), .s10(div1_1_s7[3]),
    .s9(div1_1_s7[2]), .s8(div1_1_s7[1]), .s7(div1_1_s7[0]), .s3(div1_1_s0[3]), .s2(div1_1_s0[2]),
    .s1(div1_1_s0[1]), .s0(div1_1_s0[0]));  // open: s13, s12, s11, s6, s5, s4
  J_K_Flip_Flop #(.trigger("falling")) q2 (
    .J(1'b1), .clk(q3_q), .K(1'b1), .Q(q2_q), .reset(and_2_out));  // open: Qn, preset, en
  J_K_Flip_Flop #(.trigger("falling")) q3_2 (
    .J(1'b1), .clk(out_3), .K(1'b1), .Q(out_4), .reset(and_1_out));  // open: Qn, preset, en
  J_K_Flip_Flop #(.trigger("falling")) q2_2 (
    .J(1'b1), .clk(out_4), .K(1'b1), .Q(out_5), .reset(and_1_out));  // open: Qn, preset, en
  J_K_Flip_Flop #(.trigger("falling")) q1 (
    .J(1'b1), .clk(q2_q), .K(1'b1), .Q(q1_q), .reset(and_2_out));  // open: Qn, preset, en
  div2 div2_1 (
    .a4(q0_q), .a3(q1_q), .a2(q2_q), .a1(q3_q), .a0(q4_q), .s9(div2_1_s9), .s8(div2_1_s5[3]),
    .s7(div2_1_s5[2]), .s6(div2_1_s5[1]), .s5(div2_1_s5[0]), .s4(div2_1_s4), .s3(div2_1_s0[3]),
    .s2(div2_1_s0[2]), .s1(div2_1_s0[1]), .s0(div2_1_s0[0]));
  J_K_Flip_Flop #(.trigger("falling")) q0 (
    .J(1'b1), .clk(q1_q), .K(1'b1), .Q(q0_q), .reset(and_2_out));  // open: Qn, preset, en
  J_K_Flip_Flop #(.trigger("falling")) q1_2 (
    .J(1'b1), .clk(out_5), .K(1'b1), .Q(out_6), .reset(and_1_out));  // open: Qn, preset, en
  J_K_Flip_Flop #(.trigger("falling")) q0_2 (
    .J(1'b1), .clk(out_6), .K(1'b1), .Q(out_7), .reset(and_1_out));  // open: Qn, preset, en
  Hex_Digit_Display hex_digit_display_1 (.value(div2_1_s5));  // open: dp
  Clock clock_1 (.out(clock_1_out));
  and and_3 (and_3_out, ~out_14, out_13, out_12, out_11, out_10, ~out_9, ~out_8);  // AND_Gate
  Hex_Digit_Display hex_digit_display_2 (.value(div2_1_s0));  // open: dp
  J_K_Flip_Flop #(.trigger("falling")) q6_2 (
    .J(1'b1), .clk(clock_1_out), .K(1'b1), .Q(out_8), .reset(and_3_out));  // open: Qn, preset, en
  Hex_Digit_Display hex_digit_display_3 (.value(div1_1_s0));  // open: dp
  Hex_Digit_Display hex_digit_display_4 (.value(div1_1_s7));  // open: dp
  J_K_Flip_Flop #(.trigger("falling")) q5_2 (
    .J(1'b1), .clk(out_8), .K(1'b1), .Q(out_9), .reset(and_3_out));  // open: Qn, preset, en
  Hex_Digit_Display hex_digit_display_5 (.value(div1_2_s7));  // open: dp
  Hex_Digit_Display hex_digit_display_6 (.value(div1_2_s0));  // open: dp
  J_K_Flip_Flop #(.trigger("falling")) q4_3 (
    .J(1'b1), .clk(out_9), .K(1'b1), .Q(out_10), .reset(and_3_out));  // open: Qn, preset, en
  J_K_Flip_Flop #(.trigger("falling")) q3_3 (
    .J(1'b1), .clk(out_10), .K(1'b1), .Q(out_11), .reset(and_3_out));  // open: Qn, preset, en
  div1 div1_2 (
    .a6(out_14), .a5(out_13), .a4(out_12), .a3(out_11), .a2(out_10), .a1(out_9), .a0(out_8),
    .s10(div1_2_s7[3]), .s9(div1_2_s7[2]), .s8(div1_2_s7[1]), .s7(div1_2_s7[0]), .s3(div1_2_s0[3]),
    .s2(div1_2_s0[2]), .s1(div1_2_s0[1]), .s0(div1_2_s0[0]));  // open: s13, s12, s11, s6, s5, s4
  J_K_Flip_Flop #(.trigger("falling")) q2_3 (
    .J(1'b1), .clk(out_11), .K(1'b1), .Q(out_12), .reset(and_3_out));  // open: Qn, preset, en
  J_K_Flip_Flop #(.trigger("falling")) q1_3 (
    .J(1'b1), .clk(out_12), .K(1'b1), .Q(out_13), .reset(and_3_out));  // open: Qn, preset, en
  J_K_Flip_Flop #(.trigger("falling")) q0_3 (
    .J(1'b1), .clk(out_13), .K(1'b1), .Q(out_14), .reset(and_3_out));  // open: Qn, preset, en
endmodule

module div1 (
  input  a6,
  input  a5,
  input  a4,
  input  a3,
  input  a2,
  input  a1,
  input  a0,
  output s13,
  output s12,
  output s11,
  output s10,
  output s9,
  output s8,
  output s7,
  output s6,
  output s5,
  output s4,
  output s3,
  output s2,
  output s1,
  output s0
);

  Divider #(.width(7)) divider_1 (
    .a({a6, a5, a4, a3, a2, a1, a0}), .b(7'b0001010), .out({s13, s12, s11, s10, s9, s8, s7}),
    .rem({s6, s5, s4, s3, s2, s1, s0}));  // open: upper
endmodule

module div2 (
  input  a4,
  input  a3,
  input  a2,
  input  a1,
  input  a0,
  output s9,
  output s8,
  output s7,
  output s6,
  output s5,
  output s4,
  output s3,
  output s2,
  output s1,
  output s0
);

  Divider #(.width(5)) divider_1 (
    .a({a4, a3, a2, a1, a0}), .b(5'b01010), .out({s9, s8, s7, s6, s5}), .rem({s4, s3, s2, s1, s0}));  // open: upper
endmodule
