// Logisim project cl.circ as structural Verilog
module soma (
  input  a,
  input  b,
  input  cin,
  output s
);

  wire xor_2_out;

  xor xor_1 (s, a, xor_2_out);
  xor xor_2 (xor_2_out, b, cin);
endmodule

module pgs (
  input  a,
  input  b,
  output p,
  output g
);

  or or_1 (p, a, b);
  and and_1 (g, a, b);
endmodule

module cl (
  input  a0,
  input  b0,
  input  a1,
  input  b1,
  input  a2,
  input  b2,
  input  a3,
  input  b3,
  output s3,
  output s2,
  output s1,
  output s0
);

  wire and_1_out, and_2_out, and_3_out, or_1_out, or_2_out, pg0_g, pg1_g, pg1_p, pg2_g, pg2_p;

  pgs pg2 (.a(a2), .b(b2), .p(pg2_p), .g(pg2_g));
  and and_1 (and_1_out, pg2_p, pg1_p, pg0_g);
  and and_2 (and_2_out, pg1_g, pg2_p);
  or or_1 (or_1_out, and_1_out, pg2_g, and_2_out);
  soma soma3 (.a(a3), .b(b3), .cin(or_1_out), .s(s3));
  pgs pg1 (.a(a1), .b(b1), .p(pg1_p), .g(pg1_g));
  and and_3 (and_3_out, pg1_p, pg0_g);
  or or_2 (or_2_out, pg1_g, and_3_out);
  soma soma2 (.a(a2), .b(b2), .cin(or_2_out), .s(s2));
  pgs pg0 (.a(a0), .b(b0), .g(pg0_g));  // open: p
  soma soma1 (.a(a1), .b(b1), .cin(pg0_g), .s(s1));
  soma soma0 (.a(a0), .b(b0), .cin(1'b0), .s(s0));
endmodule
