// Logisim project somasubtrai.circ as structural Verilog: 6 circuits, main circuit main
module main (
  input  a0,
  input  b0,
  input  cin,
  input  a1,
  input  b1,
  input  a2,
  input  b2,
  input  a3,
  input  b3,
  input  a4,
  input  b4,
  input  a5,
  input  b5,
  input  a6,
  input  b6,
  input  a7,
  input  b7,
  output out_18,
  output out_19,
  output out_20,
  output out_21,
  output out_22,
  output out_23,
  output out_24,
  output out_25,
  output out_26
);

  wire soma_1_c, soma_2_c, soma_3_c, soma_4_c, soma_5_c, soma_6_c, soma_7_c;

  soma soma_1 (.a(a0), .b(b0), .cin(cin), .s(out_18), .c(soma_1_c));
  soma soma_2 (.a(a1), .b(b1), .cin(soma_1_c), .s(out_19), .c(soma_2_c));
  soma soma_3 (.a(a2), .b(b2), .cin(soma_2_c), .s(out_20), .c(soma_3_c));
  soma soma_4 (.a(a3), .b(b3), .cin(soma_3_c), .s(out_21), .c(soma_4_c));
  soma soma_5 (.a(a4), .b(b4), .cin(soma_4_c), .s(out_22), .c(soma_5_c));
  soma soma_6 (.a(a5), .b(b5), .cin(soma_5_c), .s(out_23), .c(soma_6_c));
  soma soma_7 (.a(a6), .b(b6), .cin(soma_6_c), .s(out_24), .c(soma_7_c));
  soma soma_8 (.a(a7), .b(b7), .cin(soma_7_c), .s(out_25), .c(out_26));
endmodule

module soma (
  input  a,
  input  b,
  input  cin,
  output s,
  output c
);

  wire and_1_out, and_2_out, and_3_out, and_4_out, and_5_out, and_6_out, and_7_out, not_1_out, not_2_out,
       not_3_out, not_4_out, not_5_out, not_6_out, not_7_out, not_8_out;

  not not_1 (not_1_out, b);
  not not_2 (not_2_out, cin);
  not not_3 (not_3_out, a);
  not not_4 (not_4_out, b);
  not not_5 (not_5_out, a);
  not not_6 (not_6_out, cin);
  not not_7 (not_7_out, cin);
  not not_8 (not_8_out, b);
  and and_1 (and_1_out, a, b, cin);
  and and_2 (and_2_out, a, not_1_out, not_2_out);
  and and_3 (and_3_out, not_3_out, not_4_out, cin);
  and and_4 (and_4_out, not_5_out, b, not_6_out);
  and and_5 (and_5_out, b, cin);
  and and_6 (and_6_out, a, b, not_7_out);
  and and_7 (and_7_out, a, not_8_out, cin);
  or or_1 (s, and_1_out, and_2_out, and_3_out, and_4_out);
  or or_2 (c, and_5_out, and_6_out, and_7_out);
endmodule

module subtrai (
  input  a0,
  input  b0,
  input  cin,
  input  a,
  input  b,
  input  c,
  input  a1,
  input  b1,
  input  a2,
  input  b2,
  input  a3,
  input  b3,
  input  a4,
  input  b4,
  input  a5,
  input  b5,
  input  a6,
  input  b6,
  input  a7,
  input  b7,
  input  a3_2,
  input  b3_2,
  input  a2_2,
  input  b2_2,
  input  a1_2,
  input  b1_2,
  input  a0_2,
  input  b0_2,
  input  c0,
  input  a7_2,
  input  b7_2,
  input  a6_2,
  input  b6_2,
  input  a5_2,
  input  b5_2,
  input  a4_2,
  input  b4_2,
  input  a7_3,
  input  b7_3,
  input  a6_3,
  input  b6_3,
  input  a5_3,
  input  b5_3,
  input  a4_3,
  input  b4_3,
  input  a3_3,
  input  b3_3,
  input  a2_3,
  input  b2_3,
  input  a1_3,
  input  b1_3,
  input  a0_3,
  input  b0_3,
  input  c0_2,
  output out_55,
  output out_56,
  output s,
  output out_58,
  output cout,
  output out_60,
  output out_61,
  output out_62,
  output s_2,
  output s_3,
  output s_4,
  output s_5,
  output out_67,
  output out_68,
  output s_6,
  output s_7,
  output s_8,
  output s_9,
  output out_73,
  output cout_2,
  output s_10,
  output s_11,
  output s_12,
  output s_13,
  output s_14,
  output s_15,
  output s_16,
  output s_17,
  output cout_3
);

  wire and_1_out, and_2_out, and_3_out, and_4_out, and_5_out, and_6_out, mux_1_p1, mux_2_p2, mux_3_p1,
       mux_4_p1, mux_5_p1, mux_6_p2, mux_7_p2, mux_8_p2, not_1_out, not_2_out, not_3_out, not_4_out,
       not_5_out, not_6_out, not_7_out, not_8_out, not_9_out, not_10_out, not_11_out, not_12_out, not_13_out,
       not_14_out, not_15_out, soma_2_c, soma_3_c, soma_4_c, soma_5_c, soma_6_c, soma_7_c, soma_8_c,
       soma_9_c, soma_10_c, soma_11_c, soma_12_c, soma_13_c, soma_15_c, soma_16_c, somador_1_cout,
       somador_3_cout, somador_4_cout, somador_5_cout, somador_6_cout, somador_7_cout, somador_8_cout,
       xor_1_out, xor_2_out, xor_3_out, xor_4_out, xor_5_out, xor_6_out, xor_7_out, xor_8_out, xor_9_out,
       xor_10_out, xor_11_out, xor_12_out, xor_13_out, xor_14_out, xor_15_out, xor_16_out;

  somador somador_1 (.a(a3_2), .b(xor_1_out), .cin(somador_3_cout), .s(s_2), .cout(somador_1_cout));
  somador somador_2 (.a(a7_2), .b(xor_2_out), .cin(somador_4_cout), .s(s_6), .cout(cout_2));
  not not_1 (not_1_out, b);
  not not_2 (not_2_out, c);
  not not_3 (not_3_out, a);
  not not_4 (not_4_out, a);
  not not_5 (not_5_out, b);
  not not_6 (not_6_out, a);
  not not_7 (not_7_out, c);
  somador somador_3 (.a(a2_2), .b(xor_3_out), .cin(somador_5_cout), .s(s_3), .cout(somador_3_cout));
  xor xor_1 (xor_1_out, b3_2, c0);
  somador somador_4 (.a(a6_2), .b(xor_4_out), .cin(somador_6_cout), .s(s_7), .cout(somador_4_cout));
  xor xor_2 (xor_2_out, b7_2, c0);
  not not_8 (not_8_out, b7_3);
  // mux mux_1: pin names not known; wires that end beside it: mux_1_p1, not_8_out, b7_3, a5_3
  soma soma_1 (.a(a7_3), .b(mux_1_p1), .cin(soma_2_c), .s(s_10), .c(cout_3));
  and and_1 (and_1_out, a, b, c);
  and and_2 (and_2_out, a, not_1_out, not_2_out);
  and and_3 (and_3_out, not_3_out, b, c);
  and and_4 (and_4_out, not_4_out, not_5_out, c);
  and and_5 (and_5_out, b, c);
  and and_6 (and_6_out, not_6_out, b, not_7_out);
  xor xor_3 (xor_3_out, b2_2, c0);
  xor xor_4 (xor_4_out, b6_2, c0);
  not not_9 (not_9_out, b6_3);
  or or_1 (s, and_1_out, and_2_out, and_3_out, and_4_out);
  or or_2 (cout, and_4_out, and_5_out, and_6_out);
  somador somador_5 (.a(a1_2), .b(xor_5_out), .cin(somador_7_cout), .s(s_4), .cout(somador_5_cout));
  somador somador_6 (.a(a5_2), .b(xor_6_out), .cin(somador_8_cout), .s(s_8), .cout(somador_6_cout));
  // mux mux_2: pin names not known; wires that end beside it: not_9_out, mux_2_p2, not_9_out, b6_3, a5_3
  soma soma_2 (.a(a6_3), .b(mux_2_p2), .cin(soma_3_c), .s(s_11), .c(soma_2_c));
  somador somador_7 (.a(a0_2), .b(xor_8_out), .cin(c0), .s(s_5), .cout(somador_7_cout));
  xor xor_5 (xor_5_out, b1_2, c0);
  somador somador_8 (.a(a4_2), .b(xor_7_out), .cin(somador_1_cout), .s(s_9), .cout(somador_8_cout));
  xor xor_6 (xor_6_out, b5_2, c0);
  not not_10 (not_10_out, b5_3);
  // mux mux_3: pin names not known; wires that end beside it: mux_3_p1, not_10_out, b5_3, a5_3
  soma soma_3 (.a(a5_3), .b(mux_3_p1), .cin(soma_4_c), .s(s_12), .c(soma_3_c));
  xor xor_7 (xor_7_out, b4_2, c0);
  xor xor_8 (xor_8_out, c0, c0);
  not not_11 (not_11_out, b4_3);
  // mux mux_4: pin names not known; wires that end beside it: mux_4_p1, not_11_out, b4_3, a5_3
  soma soma_4 (.a(a4_3), .b(mux_4_p1), .cin(soma_5_c), .s(s_13), .c(soma_4_c));
  xor xor_9 (xor_9_out, b0, cin);
  xor xor_10 (xor_10_out, b1, cin);
  not not_12 (not_12_out, b3_3);
  // mux mux_5: pin names not known; wires that end beside it: mux_5_p1, not_12_out, b3_3, a5_3
  soma soma_5 (.a(a3_3), .b(mux_5_p1), .cin(soma_11_c), .s(s_14), .c(soma_5_c));
  soma soma_6 (.a(a0), .b(xor_9_out), .cin(cin), .s(out_55), .c(soma_6_c));
  xor xor_11 (xor_11_out, b2, cin);
  xor xor_12 (xor_12_out, b3, cin);
  xor xor_13 (xor_13_out, b4, cin);
  xor xor_14 (xor_14_out, b5, cin);
  xor xor_15 (xor_15_out, b6, cin);
  xor xor_16 (xor_16_out, b7, cin);
  not not_13 (not_13_out, b2_3);
  soma soma_7 (.a(a1), .b(xor_10_out), .cin(soma_6_c), .s(out_56), .c(soma_7_c));
  soma soma_8 (.a(a2), .b(xor_11_out), .cin(soma_7_c), .s(out_58), .c(soma_8_c));
  soma soma_9 (.a(a3), .b(xor_12_out), .cin(soma_8_c), .s(out_60), .c(soma_9_c));
  soma soma_10 (.a(a4), .b(xor_13_out), .cin(soma_9_c), .s(out_61), .c(soma_10_c));
  // mux mux_6: pin names not known; wires that end beside it: not_13_out, mux_6_p2, not_13_out, b2_3, a5_3
  soma soma_11 (.a(a2_3), .b(mux_6_p2), .cin(soma_15_c), .s(s_15), .c(soma_11_c));
  soma soma_12 (.a(a5), .b(xor_14_out), .cin(soma_10_c), .s(out_62), .c(soma_12_c));
  soma soma_13 (.a(a6), .b(xor_15_out), .cin(soma_12_c), .s(out_67), .c(soma_13_c));
  soma soma_14 (.a(a7), .b(xor_16_out), .cin(soma_13_c), .s(out_68), .c(out_73));
  not not_14 (not_14_out, b1_3);
  // mux mux_7: pin names not known; wires that end beside it: not_14_out, mux_7_p2, not_14_out, b1_3, a5_3
  soma soma_15 (.a(a1_3), .b(mux_7_p2), .cin(soma_16_c), .s(s_16), .c(soma_15_c));
  not not_15 (not_15_out, b0_3);
  // mux mux_8: pin names not known; wires that end beside it: not_15_out, mux_8_p2, not_15_out, b0_3, a5_3
  soma soma_16 (.a(a0_3), .b(mux_8_p2), .cin(a5_3), .s(s_17), .c(soma_16_c));

  assign c0_2 = a5_3;
endmodule

module somador (
  input  a,
  input  b,
  input  cin,
  output s,
  output cout
);

  wire and_1_out, and_2_out, and_3_out, xor_1_out;

  xor xor_1 (xor_1_out, b, cin);
  and and_1 (and_1_out, b, cin);
  and and_2 (and_2_out, a, b);
  and and_3 (and_3_out, a, cin);
  xor xor_2 (s, a, xor_1_out);
  or or_1 (cout, and_1_out, and_2_out, and_3_out);
endmodule

module mux (
  input  minus_b,
  input  b,
  input  c,
  output s
);

  wire and_1_out, and_2_out, not_1_out;

  and and_1 (and_1_out, minus_b, c);
  and and_2 (and_2_out, b, not_1_out);
  not not_1 (not_1_out, c);
  or or_1 (s, and_1_out, and_2_out);
endmodule

module subtraimux (
  input  c0,
  input  a3,
  input  b3,
  input  a2,
  input  b2,
  input  a1,
  input  b1,
  input  a0,
  input  b0,
  input  a7,
  input  b7,
  input  a6,
  input  b6,
  input  a5,
  input  b5,
  input  a4,
  input  b4,
  output s,
  output s_2,
  output s_3,
  output s_4,
  output cout,
  output s_5,
  output s_6,
  output s_7,
  output s_8
);

  wire mux_1_s, mux_2_s, mux_3_s, mux_4_s, mux_5_s, mux_6_s, mux_7_s, mux_8_s, not_1_out, not_2_out,
       not_3_out, not_4_out, not_5_out, not_6_out, not_7_out, not_8_out, somador_1_cout, somador_3_cout,
       somador_4_cout, somador_5_cout, somador_6_cout, somador_7_cout, somador_8_cout;

  not not_1 (not_1_out, b3);
  mux mux_1 (.minus_b(not_1_out), .b(b3), .c(c0), .s(mux_1_s));
  somador somador_1 (.a(a3), .b(mux_1_s), .cin(somador_3_cout), .s(s), .cout(somador_1_cout));
  not not_2 (not_2_out, b7);
  mux mux_2 (.minus_b(not_2_out), .b(b7), .c(c0), .s(mux_2_s));
  somador somador_2 (.a(a7), .b(mux_2_s), .cin(somador_4_cout), .s(s_5), .cout(cout));
  not not_3 (not_3_out, b2);
  mux mux_3 (.minus_b(not_3_out), .b(b2), .c(c0), .s(mux_3_s));
  not not_4 (not_4_out, b6);
  mux mux_4 (.minus_b(not_4_out), .b(b6), .c(c0), .s(mux_4_s));
  somador somador_3 (.a(a2), .b(mux_3_s), .cin(somador_5_cout), .s(s_2), .cout(somador_3_cout));
  somador somador_4 (.a(a6), .b(mux_4_s), .cin(somador_6_cout), .s(s_6), .cout(somador_4_cout));
  not not_5 (not_5_out, b1);
  mux mux_5 (.minus_b(not_5_out), .b(b1), .c(c0), .s(mux_5_s));
  somador somador_5 (.a(a1), .b(mux_5_s), .cin(somador_7_cout), .s(s_3), .cout(somador_5_cout));
  not not_6 (not_6_out, b5);
  mux mux_6 (.minus_b(not_6_out), .b(b5), .c(c0), .s(mux_6_s));
  somador somador_6 (.a(a5), .b(mux_6_s), .cin(somador_8_cout), .s(s_7), .cout(somador_6_cout));
  not not_7 (not_7_out, b0);
  mux mux_7 (.minus_b(not_7_out), .b(b0), .c(c0), .s(mux_7_s));
  somador somador_7 (.a(a0), .b(mux_7_s), .cin(c0), .s(s_4), .cout(somador_7_cout));
  not not_8 (not_8_out, b4);
  mux mux_8 (.minus_b(not_8_out), .b(b4), .c(c0), .s(mux_8_s));
  somador somador_8 (.a(a4), .b(mux_8_s), .cin(somador_1_cout), .s(s_8), .cout(somador_8_cout));
endmodule
