// Logisim project comp.circ as structural Verilog: 7 circuits, main circuit logUnit
module main (
  input  [3:0] a,
  input  [3:0] b,
  input  cin_sum,
  input  [2:0] fs,
  input  cin_sub,
  output [3:0] out_6,
  output cout_sum,
  output cout_sub,
  output [3:0] sub,
  output [3:0] div,
  output [3:0] resto,
  output [3:0] mult
);

  wire decoder_1_codes0, decoder_1_codes1, decoder_1_codes2, decoder_1_codes3, decoder_1_codes4,
       decoder_1_codes5, soma_1_cout, soma_2_cout, soma_3_cout;
  wire [3:0] logunit_1_sa, logunit_1_sb, logunit_1_units3, soma_1_sum;

  decoder decoder_1 (
    .f2(fs[2]), .f1(fs[1]), .f0(fs[0]), .codeS0(decoder_1_codes0), .codeS1(decoder_1_codes1),
    .codeS2(decoder_1_codes2), .codeS3(decoder_1_codes3), .codeS4(decoder_1_codes4), .codeS5(decoder_1_codes5));  // open: codeS6, codeS7
  logUnit logunit_1 (
    .a(a), .b(b), .SA(logunit_1_sa), .SB(logunit_1_sb), .inDecoder0(decoder_1_codes0),
    .inDecoder1(decoder_1_codes1), .inDecoder2(decoder_1_codes2), .inDecoder3(decoder_1_codes3),
    .uitS0(logunit_1_units3[3]), .unitS1(logunit_1_units3[2]), .unitS2(logunit_1_units3[1]),
    .unitS3(logunit_1_units3[0]));
  Multiplier #(.width(4)) multiplier_1 (.a(logunit_1_sa), .b(logunit_1_sb), .out(mult));  // open: cin, cout
  soma soma_1 (
    .a(logunit_1_sa[0]), .b(logunit_1_sb[0]), .e0(decoder_1_codes4), .cin(cin_sum), .sum(soma_1_sum[0]),
    .cout(soma_1_cout));
  sub sub_1 (
    .c0(cin_sub), .e0(decoder_1_codes5), .cout(cout_sub), .a3(logunit_1_sa[3]), .b3(logunit_1_sb[3]),
    .a2(logunit_1_sa[2]), .b2(logunit_1_sb[2]), .a1(logunit_1_sa[1]), .b1(logunit_1_sb[1]),
    .a0(logunit_1_sa[0]), .b0(logunit_1_sb[0]), .s3(sub[3]), .s2(sub[2]), .s1(sub[1]), .s0(sub[0]));
  Divider #(.width(4)) divider_1 (.a(logunit_1_sa), .b(logunit_1_sb), .out(div), .rem(resto));  // open: upper
  soma soma_2 (
    .a(logunit_1_sa[1]), .b(logunit_1_sb[1]), .e0(decoder_1_codes4), .cin(soma_1_cout), .sum(soma_1_sum[1]),
    .cout(soma_2_cout));
  soma soma_3 (
    .a(logunit_1_sa[2]), .b(logunit_1_sb[2]), .e0(decoder_1_codes4), .cin(soma_2_cout), .sum(soma_1_sum[2]),
    .cout(soma_3_cout));
  soma soma_4 (
    .a(logunit_1_sa[3]), .b(logunit_1_sb[3]), .e0(decoder_1_codes4), .cin(soma_3_cout), .sum(soma_1_sum[3]),
    .cout(cout_sum));
  assign out_6 = logunit_1_units3 | soma_1_sum | sub | div | resto | mult;  // OR_Gate or_1, 4 bits wide
endmodule

module decoder (
  input  f2,
  input  f1,
  input  f0,
  output codeS0,
  output codeS1,
  output codeS2,
  output codeS3,
  output codeS4,
  output codeS5,
  output codeS6,
  output codeS7
);

  wire not_1_out, not_2_out, not_3_out, not_4_out, not_5_out, not_6_out, not_7_out, not_8_out, not_9_out,
       not_10_out, not_11_out, not_12_out;

  not not_1 (not_1_out, f2);
  not not_2 (not_2_out, f2);
  not not_3 (not_3_out, f1);
  not not_4 (not_4_out, f0);
  not not_5 (not_5_out, f2);
  not not_6 (not_6_out, f1);
  not not_7 (not_7_out, f0);
  not not_8 (not_8_out, f2);
  not not_9 (not_9_out, f1);
  not not_10 (not_10_out, f0);
  not not_11 (not_11_out, f1);
  not not_12 (not_12_out, f0);
  and and_1 (codeS0, not_2_out, not_3_out, not_4_out);
  and and_2 (codeS1, not_5_out, not_6_out, f0);
  and and_3 (codeS2, not_1_out, f1, not_7_out);
  and and_4 (codeS3, not_8_out, f1, f0);
  and and_5 (codeS4, f2, not_9_out, not_10_out);
  and and_6 (codeS5, f2, not_11_out, f0);
  and and_7 (codeS6, f2, f1, not_12_out);
  and and_8 (codeS7, f2, f1, f0);
endmodule

module logUnit (
  input  [3:0] a,
  input  inDecoder0,
  input  [3:0] b,
  input  inDecoder1,
  input  inDecoder2,
  input  inDecoder3,
  output uitS0,
  output unitS1,
  output unitS2,
  output unitS3,
  output [3:0] SA,
  output [3:0] SB
);

  wire and_1_out, not_1_out, not_2_out, not_3_out, not_4_out, or_1_out, or_2_out, xor_1_out;

  not not_1 (not_1_out, b[0]);
  not not_2 (not_2_out, b[1]);
  and and_1 (and_1_out, a[0], b[0], a[1], b[1], a[2], b[2], a[3], b[3]);
  or or_1 (or_1_out, a[0], b[0], a[1], b[1], a[2], b[2], a[3], b[3]);
  or or_2 (or_2_out, not_1_out, not_2_out, not_3_out, not_4_out);
  not not_3 (not_3_out, b[2]);
  not not_4 (not_4_out, b[3]);
  ExactlyOne xor_1 (
    .out(xor_1_out), .in0(a[0]), .in1(b[0]), .in2(a[1]), .in3(b[1]), .in4(a[2]), .in5(b[2]), .in6(a[3]),
    .in7(b[3]));
  and and_2 (uitS0, and_1_out, inDecoder0);
  and and_3 (unitS1, or_1_out, inDecoder1);
  and and_4 (unitS2, or_2_out, inDecoder2);
  and and_5 (unitS3, xor_1_out, inDecoder3);

  assign SA = a;
  assign SB = a;
endmodule

module soma (
  input  cin,
  input  a,
  input  b,
  input  e0,
  output sum,
  output cout
);

  wire and_1_out, and_2_out, xor_1_out, xor_2_out;

  and and_1 (and_1_out, e0, b, a);
  xor xor_1 (xor_1_out, a, b);
  or or_1 (cout, and_1_out, and_2_out);
  and and_2 (and_2_out, e0, xor_1_out, cin);
  xor xor_2 (xor_2_out, cin, xor_1_out);
  and and_3 (sum, xor_2_out, e0);
endmodule

module sub (
  input  a3,
  input  b3,
  input  a2,
  input  b2,
  input  a1,
  input  b1,
  input  a0,
  input  b0,
  input  c0,
  input  e0,
  output cout,
  output s3,
  output s2,
  output s1,
  output s0
);

  wire and_1_out, mux_1_s, mux_2_s, mux_3_s, mux_4_s, not_1_out, not_2_out, not_3_out, not_4_out,
       somador_2_cout, somador_3_cout, somador_4_cout;

  and and_1 (and_1_out, c0, e0);
  not not_1 (not_1_out, b3);
  mux mux_1 (.minus_b(not_1_out), .b(b3), .c(and_1_out), .s(mux_1_s));
  somador somador_1 (.a(a3), .b(mux_1_s), .cin(somador_2_cout), .s(s3), .cout(cout));
  not not_2 (not_2_out, b2);
  mux mux_2 (.minus_b(not_2_out), .b(b2), .c(and_1_out), .s(mux_2_s));
  somador somador_2 (.a(a2), .b(mux_2_s), .cin(somador_3_cout), .s(s2), .cout(somador_2_cout));
  not not_3 (not_3_out, b1);
  mux mux_3 (.minus_b(not_3_out), .b(b1), .c(and_1_out), .s(mux_3_s));
  somador somador_3 (.a(a1), .b(mux_3_s), .cin(somador_4_cout), .s(s1), .cout(somador_3_cout));
  not not_4 (not_4_out, b0);
  mux mux_4 (.minus_b(not_4_out), .b(b0), .c(and_1_out), .s(mux_4_s));
  somador somador_4 (.a(a0), .b(mux_4_s), .cin(and_1_out), .s(s0), .cout(somador_4_cout));
endmodule

module mux (
  input  minus_b,
  input  b,
  input  c,
  output s
);

  wire and_1_out, and_2_out, not_1_out;

  and and_1 (and_1_out, minus_b, c);
  and and_2 (and_2_out, b, not_1_out);
  not not_1 (not_1_out, c);
  or or_1 (s, and_1_out, and_2_out);
endmodule

module somador (
  input  a,
  input  b,
  input  cin,
  output s,
  output cout
);

  wire and_1_out, and_2_out, and_3_out, xor_1_out;

  xor xor_1 (xor_1_out, b, cin);
  and and_1 (and_1_out, b, cin);
  and and_2 (and_2_out, a, b);
  and and_3 (and_3_out, a, cin);
  xor xor_2 (s, a, xor_1_out);
  or or_1 (cout, and_1_out, and_2_out, and_3_out);
endmodule
