// Logisim project comp.circ as structural Verilog: 11 circuits, main circuit main
module main (
  input  [7:0] a,
  input  [7:0] b,
  input  [2:0] fs,
  output [7:0] \output ,
  output cout_sum,
  output cout_sub,
  output [7:0] sub,
  output [7:0] div,
  output [7:0] resto,
  output [7:0] mult
);

  wire decoder_1_codes0, decoder_1_codes1, decoder_1_codes2, decoder_1_codes4, soma_1_cout, soma_2_cout,
       soma_3_cout, soma_4_cout, soma_5_cout, soma_6_cout, soma_7_cout;
  wire [7:0] and_1_out, and_2_out, and_3_out, and_4_out, logunit_1_sa, logunit_1_sb, logunit_1_uits0,
       logunit_1_units1, logunit_1_units3, soma_1_sum;
  wire [7:7] decoder_1_codes3, decoder_1_codes5, decoder_1_codes6, decoder_1_codes7;

  decoder decoder_1 (
    .f2(fs[2]), .f1(fs[1]), .f0(fs[0]), .codeS0(decoder_1_codes0), .codeS1(decoder_1_codes1),
    .codeS2(decoder_1_codes2), .codeS3(decoder_1_codes3[7]), .codeS4(decoder_1_codes4),
    .codeS5(decoder_1_codes5[7]), .codeS6(decoder_1_codes6[7]), .codeS7(decoder_1_codes7[7]));
  logUnit logunit_1 (
    .a(a), .b(b), .SA(logunit_1_sa), .SB(logunit_1_sb), .inDecoder0(decoder_1_codes0),
    .inDecoder1(decoder_1_codes1), .inDecoder3(decoder_1_codes2), .uitS0(logunit_1_uits0),
    .unitS1(logunit_1_units1), .unitS3(logunit_1_units3));
  Multiplier multiplier_1 (.a(logunit_1_sa), .b(logunit_1_sb), .out(mult));  // open: cin, cout
  sub sub_1 (
    .cout(cout_sub), .a3(logunit_1_sb[3]), .a7(logunit_1_sb[7]), .b3(logunit_1_sa[3]), .b7(logunit_1_sa[7]),
    .a2(logunit_1_sb[2]), .a6(logunit_1_sb[6]), .b2(logunit_1_sa[2]), .b6(logunit_1_sa[6]),
    .a1(logunit_1_sb[1]), .a5(logunit_1_sb[5]), .b1(logunit_1_sa[1]), .b5(logunit_1_sa[5]),
    .a0(logunit_1_sb[0]), .a4(logunit_1_sb[4]), .b0(logunit_1_sa[0]), .b4(logunit_1_sa[4]), .s3(sub[3]),
    .s2(sub[2]), .s1(sub[1]), .s0(sub[0]), .s7(sub[7]), .s6(sub[6]), .s5(sub[5]), .s4(sub[4]));
  Divider divider_1 (.a(logunit_1_sb), .b(logunit_1_sa), .out(div), .rem(resto));  // open: upper
  soma soma_1 (
    .a(logunit_1_sa[0]), .b(logunit_1_sb[0]), .e0(decoder_1_codes4), .cin(1'b0), .sum(soma_1_sum[0]),
    .cout(soma_1_cout));
  soma soma_2 (
    .a(logunit_1_sa[1]), .b(logunit_1_sb[1]), .e0(decoder_1_codes4), .cin(soma_1_cout), .sum(soma_1_sum[1]),
    .cout(soma_2_cout));
  soma soma_3 (
    .a(logunit_1_sa[2]), .b(logunit_1_sb[2]), .e0(decoder_1_codes4), .cin(soma_2_cout), .sum(soma_1_sum[2]),
    .cout(soma_3_cout));
  soma soma_4 (
    .a(logunit_1_sa[4]), .b(logunit_1_sb[4]), .e0(decoder_1_codes4), .cin(soma_5_cout), .sum(soma_1_sum[4]),
    .cout(soma_4_cout));
  soma soma_5 (
    .a(logunit_1_sa[3]), .b(logunit_1_sb[3]), .e0(decoder_1_codes4), .cin(soma_3_cout), .sum(soma_1_sum[3]),
    .cout(soma_5_cout));
  assign and_1_out = {8{decoder_1_codes5[7]}} & sub;  // AND_Gate and_1, 8 bits wide
  soma soma_6 (
    .a(logunit_1_sa[5]), .b(logunit_1_sb[5]), .e0(decoder_1_codes4), .cin(soma_4_cout), .sum(soma_1_sum[5]),
    .cout(soma_6_cout));
  soma soma_7 (
    .a(logunit_1_sa[6]), .b(logunit_1_sb[6]), .e0(decoder_1_codes4), .cin(soma_6_cout), .sum(soma_1_sum[6]),
    .cout(soma_7_cout));
  soma soma_8 (
    .a(logunit_1_sa[7]), .b(logunit_1_sb[7]), .e0(decoder_1_codes4), .cin(soma_7_cout), .sum(soma_1_sum[7]),
    .cout(cout_sum));
  assign \output  = logunit_1_uits0 | logunit_1_units1 | logunit_1_units3 | soma_1_sum | and_1_out | and_4_out | and_3_out | and_2_out;  // OR_Gate or_1, 8 bits wide
  assign and_2_out = mult & {8{decoder_1_codes7[7]}};  // AND_Gate and_2, 8 bits wide
  assign and_3_out = resto & {8{decoder_1_codes3[7]}};  // AND_Gate and_3, 8 bits wide
  assign and_4_out = div & {8{decoder_1_codes6[7]}};  // AND_Gate and_4, 8 bits wide

  // Notes on the sheet:
  //   000 = and
  //   001 = or
  //   010 = resto divisao
  //   011 = xor
  //   100 = adicao
  //   101 = subtracao
  //   110 = divisao
  //   111 = multiplicacao
endmodule

module decoder (
  input  f2,
  input  f1,
  input  f0,
  output codeS0,
  output codeS1,
  output codeS2,
  output codeS3,
  output codeS4,
  output codeS5,
  output codeS6,
  output codeS7
);

  wire not_1_out, not_2_out, not_3_out, not_4_out, not_5_out, not_6_out, not_7_out, not_8_out, not_9_out,
       not_10_out, not_11_out, not_12_out;

  not not_1 (not_1_out, f2);
  not not_2 (not_2_out, f2);
  not not_3 (not_3_out, f1);
  not not_4 (not_4_out, f0);
  not not_5 (not_5_out, f2);
  not not_6 (not_6_out, f1);
  not not_7 (not_7_out, f0);
  not not_8 (not_8_out, f2);
  not not_9 (not_9_out, f1);
  not not_10 (not_10_out, f0);
  not not_11 (not_11_out, f1);
  not not_12 (not_12_out, f0);
  and and_1 (codeS0, not_2_out, not_3_out, not_4_out);
  and and_2 (codeS1, not_5_out, not_6_out, f0);
  and and_3 (codeS2, not_1_out, f1, not_7_out);
  and and_4 (codeS3, not_8_out, f1, f0);
  and and_5 (codeS4, f2, not_9_out, not_10_out);
  and and_6 (codeS5, f2, not_11_out, f0);
  and and_7 (codeS6, f2, f1, not_12_out);
  and and_8 (codeS7, f2, f1, f0);
endmodule

module logUnit (
  input  [7:0] a,
  input  [7:0] b,
  input  inDecoder3,
  input  inDecoder1,
  input  inDecoder0,
  output [7:0] uitS0,
  output [7:0] unitS1,
  output [7:0] unitS3,
  output [7:0] SA,
  output [7:0] SB
);

  wire [7:0] and_1_out, or_1_out, xor_1_out;

  assign and_1_out = a & b;  // AND_Gate and_1, 8 bits wide
  assign or_1_out = a | b;  // OR_Gate or_1, 8 bits wide
  assign xor_1_out = a ^ b;  // XOR_Gate xor_1, 8 bits wide
  assign uitS0 = and_1_out & {8{inDecoder0}};  // AND_Gate and_2, 8 bits wide
  assign unitS1 = or_1_out & {8{inDecoder1}};  // AND_Gate and_3, 8 bits wide
  assign unitS3 = xor_1_out & {8{inDecoder3}};  // AND_Gate and_4, 8 bits wide

  assign SA = a;
  assign SB = b;
endmodule

module soma (
  input  cin,
  input  a,
  input  b,
  input  e0,
  output sum,
  output cout
);

  wire and_1_out, and_2_out, xor_1_out, xor_2_out;

  and and_1 (and_1_out, e0, b, a);
  xor xor_1 (xor_1_out, a, b);
  or or_1 (cout, and_1_out, and_2_out);
  and and_2 (and_2_out, e0, xor_1_out, cin);
  xor xor_2 (xor_2_out, cin, xor_1_out);
  and and_3 (sum, xor_2_out, e0);
endmodule

module sub (
  input  a3,
  input  b3,
  input  a2,
  input  b2,
  input  a1,
  input  b1,
  input  a0,
  input  b0,
  input  a7,
  input  b7,
  input  a6,
  input  b6,
  input  a5,
  input  b5,
  input  a4,
  input  b4,
  output s3,
  output s2,
  output s1,
  output s0,
  output cout,
  output s7,
  output s6,
  output s5,
  output s4
);

  wire mux_1_s, mux_2_s, mux_3_s, mux_4_s, mux_5_s, mux_6_s, mux_7_s, mux_8_s, not_1_out, not_2_out,
       not_3_out, not_4_out, not_5_out, not_6_out, not_7_out, not_8_out, somador_1_cout, somador_3_cout,
       somador_4_cout, somador_5_cout, somador_6_cout, somador_7_cout, somador_8_cout;

  not not_1 (not_1_out, b3);
  mux mux_1 (.minus_b(not_1_out), .b(b3), .c(1'b1), .s(mux_1_s));
  somador somador_1 (.a(a3), .b(mux_1_s), .cin(somador_3_cout), .s(s3), .cout(somador_1_cout));
  not not_2 (not_2_out, b7);
  mux mux_2 (.minus_b(not_2_out), .b(b7), .c(1'b1), .s(mux_2_s));
  somador somador_2 (.a(a7), .b(mux_2_s), .cin(somador_4_cout), .s(s7), .cout(cout));
  not not_3 (not_3_out, b2);
  mux mux_3 (.minus_b(not_3_out), .b(b2), .c(1'b1), .s(mux_3_s));
  not not_4 (not_4_out, b6);
  mux mux_4 (.minus_b(not_4_out), .b(b6), .c(1'b1), .s(mux_4_s));
  somador somador_3 (.a(a2), .b(mux_3_s), .cin(somador_5_cout), .s(s2), .cout(somador_3_cout));
  somador somador_4 (.a(a6), .b(mux_4_s), .cin(somador_6_cout), .s(s6), .cout(somador_4_cout));
  not not_5 (not_5_out, b1);
  mux mux_5 (.minus_b(not_5_out), .b(b1), .c(1'b1), .s(mux_5_s));
  somador somador_5 (.a(a1), .b(mux_5_s), .cin(somador_7_cout), .s(s1), .cout(somador_5_cout));
  not not_6 (not_6_out, b5);
  mux mux_6 (.minus_b(not_6_out), .b(b5), .c(1'b1), .s(mux_6_s));
  somador somador_6 (.a(a5), .b(mux_6_s), .cin(somador_8_cout), .s(s5), .cout(somador_6_cout));
  not not_7 (not_7_out, b0);
  mux mux_7 (.minus_b(not_7_out), .b(b0), .c(1'b1), .s(mux_7_s));
  somador somador_7 (.a(a0), .b(mux_7_s), .cin(1'b1), .s(s0), .cout(somador_7_cout));
  not not_8 (not_8_out, b4);
  mux mux_8 (.minus_b(not_8_out), .b(b4), .c(1'b1), .s(mux_8_s));
  somador somador_8 (.a(a4), .b(mux_8_s), .cin(somador_1_cout), .s(s4), .cout(somador_8_cout));
endmodule

module mux (
  input  minus_b,
  input  b,
  input  c,
  output s
);

  wire and_1_out, and_2_out, not_1_out;

  and and_1 (and_1_out, minus_b, c);
  and and_2 (and_2_out, b, not_1_out);
  not not_1 (not_1_out, c);
  or or_1 (s, and_1_out, and_2_out);
endmodule

module somador (
  input  a,
  input  b,
  input  cin,
  output s,
  output cout
);

  wire and_1_out, and_2_out, and_3_out, xor_1_out;

  xor xor_1 (xor_1_out, b, cin);
  and and_1 (and_1_out, b, cin);
  and and_2 (and_2_out, a, b);
  and and_3 (and_3_out, a, cin);
  xor xor_2 (s, a, xor_1_out);
  or or_1 (cout, and_1_out, and_2_out, and_3_out);
endmodule

module memoria11x8 (
  input  [10:0] Entrada,
  input  [2:0] \Endereço ,
  input  Leitura_Escrita,
  output [10:0] \Saída 
);

  wire and_1_out, and_2_out, and_3_out, and_4_out, and_5_out, and_6_out, and_7_out, and_8_out, and_9_out,
       and_10_out, and_11_out, and_12_out, and_13_out, and_14_out, and_15_out, and_16_out, and_17_out,
       and_18_out, and_19_out, and_20_out, and_21_out, and_22_out, and_23_out, and_24_out, and_25_out,
       and_26_out, and_27_out, and_28_out, and_29_out, and_30_out, and_31_out, and_32_out, and_33_out,
       and_34_out, and_35_out, and_36_out, and_37_out, and_38_out, and_39_out, and_40_out, and_41_out,
       and_42_out, and_43_out, and_44_out, and_45_out, and_46_out, and_47_out, and_48_out, and_49_out,
       and_50_out, and_51_out, and_52_out, and_53_out, and_54_out, and_55_out, and_56_out, and_57_out,
       and_58_out, and_59_out, and_60_out, and_61_out, and_62_out, and_63_out, and_64_out, and_65_out,
       and_66_out, and_67_out, and_68_out, and_69_out, and_70_out, and_71_out, and_72_out, and_73_out,
       and_74_out, and_75_out, and_76_out, and_77_out, and_78_out, and_79_out, and_80_out, and_81_out,
       and_82_out, and_83_out, and_84_out, and_85_out, and_86_out, and_87_out, and_88_out, and_89_out,
       and_90_out, and_91_out, and_92_out, and_93_out, and_94_out, and_95_out, and_96_out, and_97_out,
       and_98_out, and_99_out, and_100_out, and_101_out, and_102_out, and_103_out, and_104_out, d_ff_1_q,
       d_ff_2_q, d_ff_3_q, d_ff_4_q, d_ff_5_q, d_ff_6_q, d_ff_7_q, d_ff_8_q, d_ff_9_q, d_ff_10_q, d_ff_11_q,
       d_ff_12_q, d_ff_13_q, d_ff_14_q, d_ff_15_q, d_ff_16_q, d_ff_17_q, d_ff_18_q, d_ff_19_q, d_ff_20_q,
       d_ff_21_q, d_ff_22_q, d_ff_23_q, d_ff_24_q, d_ff_25_q, d_ff_26_q, d_ff_27_q, d_ff_28_q, d_ff_29_q,
       d_ff_30_q, d_ff_31_q, d_ff_32_q, d_ff_33_q, d_ff_34_q, d_ff_35_q, d_ff_36_q, d_ff_37_q, d_ff_38_q,
       d_ff_39_q, d_ff_40_q, d_ff_41_q, d_ff_42_q, d_ff_43_q, d_ff_44_q, d_ff_45_q, d_ff_46_q, d_ff_47_q,
       d_ff_48_q, d_ff_49_q, d_ff_50_q, d_ff_51_q, d_ff_52_q, d_ff_53_q, d_ff_54_q, d_ff_55_q, d_ff_56_q,
       d_ff_57_q, d_ff_58_q, d_ff_59_q, d_ff_60_q, d_ff_61_q, d_ff_62_q, d_ff_63_q, d_ff_64_q, d_ff_65_q,
       d_ff_66_q, d_ff_67_q, d_ff_68_q, d_ff_69_q, d_ff_70_q, d_ff_71_q, d_ff_72_q, d_ff_73_q, d_ff_74_q,
       d_ff_75_q, d_ff_76_q, d_ff_77_q, d_ff_78_q, d_ff_79_q, d_ff_80_q, d_ff_81_q, d_ff_82_q, d_ff_83_q,
       d_ff_84_q, d_ff_85_q, d_ff_86_q, d_ff_87_q, d_ff_88_q;

  and and_1 (and_1_out, ~\Endereço [2], ~\Endereço [1], ~\Endereço [0]);  // AND_Gate
  and and_2 (and_2_out, ~\Endereço [2], ~\Endereço [1], \Endereço [0]);  // AND_Gate
  and and_3 (and_3_out, ~\Endereço [2], \Endereço [1], ~\Endereço [0]);  // AND_Gate
  and and_4 (and_4_out, ~\Endereço [2], \Endereço [1], \Endereço [0]);  // AND_Gate
  and and_5 (and_5_out, \Endereço [2], ~\Endereço [1], ~\Endereço [0]);  // AND_Gate
  and and_6 (and_6_out, \Endereço [2], ~\Endereço [1], \Endereço [0]);  // AND_Gate
  and and_7 (and_7_out, \Endereço [2], \Endereço [1], ~\Endereço [0]);  // AND_Gate
  and and_8 (and_8_out, \Endereço [2], \Endereço [1], \Endereço [0]);
  and and_9 (and_9_out, and_1_out, Leitura_Escrita);
  and and_10 (and_10_out, and_2_out, Leitura_Escrita);
  and and_11 (and_11_out, and_3_out, Leitura_Escrita);
  and and_12 (and_12_out, and_4_out, Leitura_Escrita);
  and and_13 (and_13_out, and_5_out, Leitura_Escrita);
  and and_14 (and_14_out, and_6_out, Leitura_Escrita);
  and and_15 (and_15_out, and_7_out, Leitura_Escrita);
  and and_16 (and_16_out, and_8_out, Leitura_Escrita);
  D_Flip_Flop #(.trigger("falling")) d_ff_1 (
    .clk(and_9_out), .D(Entrada[10]), .Q(d_ff_1_q));  // open: Qn, preset, en, reset
  and and_17 (and_17_out, d_ff_1_q, and_1_out);
  D_Flip_Flop #(.trigger("falling")) d_ff_2 (
    .clk(and_10_out), .D(Entrada[10]), .Q(d_ff_2_q));  // open: Qn, preset, en, reset
  and and_18 (and_18_out, d_ff_2_q, and_2_out);
  D_Flip_Flop #(.trigger("falling")) d_ff_3 (
    .clk(and_11_out), .D(Entrada[10]), .Q(d_ff_3_q));  // open: Qn, preset, en, reset
  and and_19 (and_19_out, d_ff_3_q, and_3_out);
  D_Flip_Flop #(.trigger("falling")) d_ff_4 (
    .clk(and_12_out), .D(Entrada[10]), .Q(d_ff_4_q));  // open: Qn, preset, en, reset
  and and_20 (and_20_out, d_ff_4_q, and_4_out);
  D_Flip_Flop #(.trigger("falling")) d_ff_5 (
    .clk(and_13_out), .D(Entrada[10]), .Q(d_ff_5_q));  // open: Qn, preset, en, reset
  and and_21 (and_21_out, d_ff_5_q, and_5_out);
  D_Flip_Flop #(.trigger("falling")) d_ff_6 (
    .clk(and_14_out), .D(Entrada[10]), .Q(d_ff_6_q));  // open: Qn, preset, en, reset
  and and_22 (and_22_out, d_ff_6_q, and_6_out);
  D_Flip_Flop #(.trigger("falling")) d_ff_7 (
    .clk(and_15_out), .D(Entrada[10]), .Q(d_ff_7_q));  // open: Qn, preset, en, reset
  and and_23 (and_23_out, d_ff_7_q, and_7_out);
  D_Flip_Flop #(.trigger("falling")) d_ff_8 (
    .clk(and_16_out), .D(Entrada[10]), .Q(d_ff_8_q));  // open: Qn, preset, en, reset
  and and_24 (and_24_out, d_ff_8_q, and_8_out);
  or or_1 (\Saída [10], and_24_out, and_23_out, and_22_out, and_21_out, and_20_out, and_19_out, and_18_out, and_17_out);
  D_Flip_Flop #(.trigger("falling")) d_ff_9 (
    .clk(and_9_out), .D(Entrada[9]), .Q(d_ff_9_q));  // open: Qn, preset, en, reset
  and and_25 (and_25_out, d_ff_9_q, and_1_out);
  D_Flip_Flop #(.trigger("falling")) d_ff_10 (
    .clk(and_10_out), .D(Entrada[9]), .Q(d_ff_10_q));  // open: Qn, preset, en, reset
  and and_26 (and_26_out, d_ff_10_q, and_2_out);
  D_Flip_Flop #(.trigger("falling")) d_ff_11 (
    .clk(and_11_out), .D(Entrada[9]), .Q(d_ff_11_q));  // open: Qn, preset, en, reset
  and and_27 (and_27_out, d_ff_11_q, and_3_out);
  D_Flip_Flop #(.trigger("falling")) d_ff_12 (
    .clk(and_12_out), .D(Entrada[9]), .Q(d_ff_12_q));  // open: Qn, preset, en, reset
  and and_28 (and_28_out, d_ff_12_q, and_4_out);
  D_Flip_Flop #(.trigger("falling")) d_ff_13 (
    .clk(and_13_out), .D(Entrada[9]), .Q(d_ff_13_q));  // open: Qn, preset, en, reset
  and and_29 (and_29_out, d_ff_13_q, and_5_out);
  D_Flip_Flop #(.trigger("falling")) d_ff_14 (
    .clk(and_14_out), .D(Entrada[9]), .Q(d_ff_14_q));  // open: Qn, preset, en, reset
  and and_30 (and_30_out, d_ff_14_q, and_6_out);
  D_Flip_Flop #(.trigger("falling")) d_ff_15 (
    .clk(and_15_out), .D(Entrada[9]), .Q(d_ff_15_q));  // open: Qn, preset, en, reset
  and and_31 (and_31_out, d_ff_15_q, and_7_out);
  D_Flip_Flop #(.trigger("falling")) d_ff_16 (
    .clk(and_16_out), .D(Entrada[9]), .Q(d_ff_16_q));  // open: Qn, preset, en, reset
  and and_32 (and_32_out, d_ff_16_q, and_8_out);
  or or_2 (\Saída [9], and_32_out, and_31_out, and_30_out, and_29_out, and_28_out, and_27_out, and_26_out, and_25_out);
  D_Flip_Flop #(.trigger("falling")) d_ff_17 (
    .clk(and_9_out), .D(Entrada[8]), .Q(d_ff_17_q));  // open: Qn, preset, en, reset
  D_Flip_Flop #(.trigger("falling")) d_ff_18 (
    .clk(and_10_out), .D(Entrada[8]), .Q(d_ff_18_q));  // open: Qn, preset, en, reset
  D_Flip_Flop #(.trigger("falling")) d_ff_19 (
    .clk(and_11_out), .D(Entrada[8]), .Q(d_ff_19_q));  // open: Qn, preset, en, reset
  D_Flip_Flop #(.trigger("falling")) d_ff_20 (
    .clk(and_12_out), .D(Entrada[8]), .Q(d_ff_20_q));  // open: Qn, preset, en, reset
  D_Flip_Flop #(.trigger("falling")) d_ff_21 (
    .clk(and_13_out), .D(Entrada[8]), .Q(d_ff_21_q));  // open: Qn, preset, en, reset
  D_Flip_Flop #(.trigger("falling")) d_ff_22 (
    .clk(and_14_out), .D(Entrada[8]), .Q(d_ff_22_q));  // open: Qn, preset, en, reset
  D_Flip_Flop #(.trigger("falling")) d_ff_23 (
    .clk(and_15_out), .D(Entrada[8]), .Q(d_ff_23_q));  // open: Qn, preset, en, reset
  D_Flip_Flop #(.trigger("falling")) d_ff_24 (
    .clk(and_16_out), .D(Entrada[8]), .Q(d_ff_24_q));  // open: Qn, preset, en, reset
  and and_33 (and_33_out, d_ff_17_q, and_1_out);
  and and_34 (and_34_out, d_ff_18_q, and_2_out);
  and and_35 (and_35_out, d_ff_19_q, and_3_out);
  and and_36 (and_36_out, d_ff_20_q, and_4_out);
  and and_37 (and_37_out, d_ff_21_q, and_5_out);
  and and_38 (and_38_out, d_ff_22_q, and_6_out);
  and and_39 (and_39_out, d_ff_23_q, and_7_out);
  and and_40 (and_40_out, d_ff_24_q, and_8_out);
  or or_3 (\Saída [8], and_40_out, and_39_out, and_38_out, and_37_out, and_36_out, and_35_out, and_34_out, and_33_out);
  D_Flip_Flop #(.trigger("falling")) d_ff_25 (
    .clk(and_9_out), .D(Entrada[7]), .Q(d_ff_25_q));  // open: Qn, preset, en, reset
  D_Flip_Flop #(.trigger("falling")) d_ff_26 (
    .clk(and_10_out), .D(Entrada[7]), .Q(d_ff_26_q));  // open: Qn, preset, en, reset
  D_Flip_Flop #(.trigger("falling")) d_ff_27 (
    .clk(and_11_out), .D(Entrada[7]), .Q(d_ff_27_q));  // open: Qn, preset, en, reset
  D_Flip_Flop #(.trigger("falling")) d_ff_28 (
    .clk(and_12_out), .D(Entrada[7]), .Q(d_ff_28_q));  // open: Qn, preset, en, reset
  D_Flip_Flop #(.trigger("falling")) d_ff_29 (
    .clk(and_13_out), .D(Entrada[7]), .Q(d_ff_29_q));  // open: Qn, preset, en, reset
  D_Flip_Flop #(.trigger("falling")) d_ff_30 (
    .clk(and_14_out), .D(Entrada[7]), .Q(d_ff_30_q));  // open: Qn, preset, en, reset
  D_Flip_Flop #(.trigger("falling")) d_ff_31 (
    .clk(and_15_out), .D(Entrada[7]), .Q(d_ff_31_q));  // open: Qn, preset, en, reset
  D_Flip_Flop #(.trigger("falling")) d_ff_32 (
    .clk(and_16_out), .D(Entrada[7]), .Q(d_ff_32_q));  // open: Qn, preset, en, reset
  and and_41 (and_41_out, d_ff_25_q, and_1_out);
  and and_42 (and_42_out, d_ff_26_q, and_2_out);
  and and_43 (and_43_out, d_ff_27_q, and_3_out);
  and and_44 (and_44_out, d_ff_28_q, and_4_out);
  and and_45 (and_45_out, d_ff_29_q, and_5_out);
  and and_46 (and_46_out, d_ff_30_q, and_6_out);
  and and_47 (and_47_out, d_ff_31_q, and_7_out);
  and and_48 (and_48_out, d_ff_32_q, and_8_out);
  or or_4 (\Saída [7], and_48_out, and_47_out, and_46_out, and_45_out, and_44_out, and_43_out, and_42_out, and_41_out);
  D_Flip_Flop #(.trigger("falling")) d_ff_33 (
    .clk(and_9_out), .D(Entrada[6]), .Q(d_ff_33_q));  // open: Qn, preset, en, reset
  and and_49 (and_49_out, d_ff_33_q, and_1_out);
  D_Flip_Flop #(.trigger("falling")) d_ff_34 (
    .clk(and_10_out), .D(Entrada[6]), .Q(d_ff_34_q));  // open: Qn, preset, en, reset
  and and_50 (and_50_out, d_ff_34_q, and_2_out);
  D_Flip_Flop #(.trigger("falling")) d_ff_35 (
    .clk(and_11_out), .D(Entrada[6]), .Q(d_ff_35_q));  // open: Qn, preset, en, reset
  and and_51 (and_51_out, d_ff_35_q, and_3_out);
  D_Flip_Flop #(.trigger("falling")) d_ff_36 (
    .clk(and_12_out), .D(Entrada[6]), .Q(d_ff_36_q));  // open: Qn, preset, en, reset
  and and_52 (and_52_out, d_ff_36_q, and_4_out);
  D_Flip_Flop #(.trigger("falling")) d_ff_37 (
    .clk(and_13_out), .D(Entrada[6]), .Q(d_ff_37_q));  // open: Qn, preset, en, reset
  and and_53 (and_53_out, d_ff_37_q, and_5_out);
  D_Flip_Flop #(.trigger("falling")) d_ff_38 (
    .clk(and_14_out), .D(Entrada[6]), .Q(d_ff_38_q));  // open: Qn, preset, en, reset
  and and_54 (and_54_out, d_ff_38_q, and_6_out);
  D_Flip_Flop #(.trigger("falling")) d_ff_39 (
    .clk(and_15_out), .D(Entrada[6]), .Q(d_ff_39_q));  // open: Qn, preset, en, reset
  and and_55 (and_55_out, d_ff_39_q, and_7_out);
  D_Flip_Flop #(.trigger("falling")) d_ff_40 (
    .clk(and_16_out), .D(Entrada[6]), .Q(d_ff_40_q));  // open: Qn, preset, en, reset
  and and_56 (and_56_out, d_ff_40_q, and_8_out);
  or or_5 (\Saída [6], and_56_out, and_55_out, and_54_out, and_53_out, and_52_out, and_51_out, and_50_out, and_49_out);
  D_Flip_Flop #(.trigger("falling")) d_ff_41 (
    .clk(and_9_out), .D(Entrada[5]), .Q(d_ff_41_q));  // open: Qn, preset, en, reset
  and and_57 (and_57_out, d_ff_41_q, and_1_out);
  D_Flip_Flop #(.trigger("falling")) d_ff_42 (
    .clk(and_10_out), .D(Entrada[5]), .Q(d_ff_42_q));  // open: Qn, preset, en, reset
  and and_58 (and_58_out, d_ff_42_q, and_2_out);
  D_Flip_Flop #(.trigger("falling")) d_ff_43 (
    .clk(and_11_out), .D(Entrada[5]), .Q(d_ff_43_q));  // open: Qn, preset, en, reset
  and and_59 (and_59_out, d_ff_43_q, and_3_out);
  D_Flip_Flop #(.trigger("falling")) d_ff_44 (
    .clk(and_12_out), .D(Entrada[5]), .Q(d_ff_44_q));  // open: Qn, preset, en, reset
  and and_60 (and_60_out, d_ff_44_q, and_4_out);
  D_Flip_Flop #(.trigger("falling")) d_ff_45 (
    .clk(and_13_out), .D(Entrada[5]), .Q(d_ff_45_q));  // open: Qn, preset, en, reset
  and and_61 (and_61_out, d_ff_45_q, and_5_out);
  D_Flip_Flop #(.trigger("falling")) d_ff_46 (
    .clk(and_14_out), .D(Entrada[5]), .Q(d_ff_46_q));  // open: Qn, preset, en, reset
  and and_62 (and_62_out, d_ff_46_q, and_6_out);
  D_Flip_Flop #(.trigger("falling")) d_ff_47 (
    .clk(and_15_out), .D(Entrada[5]), .Q(d_ff_47_q));  // open: Qn, preset, en, reset
  and and_63 (and_63_out, d_ff_47_q, and_7_out);
  D_Flip_Flop #(.trigger("falling")) d_ff_48 (
    .clk(and_16_out), .D(Entrada[5]), .Q(d_ff_48_q));  // open: Qn, preset, en, reset
  and and_64 (and_64_out, d_ff_48_q, and_8_out);
  or or_6 (\Saída [5], and_64_out, and_63_out, and_62_out, and_61_out, and_60_out, and_59_out, and_58_out, and_57_out);
  D_Flip_Flop #(.trigger("falling")) d_ff_49 (
    .clk(and_9_out), .D(Entrada[4]), .Q(d_ff_49_q));  // open: Qn, preset, en, reset
  D_Flip_Flop #(.trigger("falling")) d_ff_50 (
    .clk(and_10_out), .D(Entrada[4]), .Q(d_ff_50_q));  // open: Qn, preset, en, reset
  D_Flip_Flop #(.trigger("falling")) d_ff_51 (
    .clk(and_11_out), .D(Entrada[4]), .Q(d_ff_51_q));  // open: Qn, preset, en, reset
  D_Flip_Flop #(.trigger("falling")) d_ff_52 (
    .clk(and_12_out), .D(Entrada[4]), .Q(d_ff_52_q));  // open: Qn, preset, en, reset
  D_Flip_Flop #(.trigger("falling")) d_ff_53 (
    .clk(and_13_out), .D(Entrada[4]), .Q(d_ff_53_q));  // open: Qn, preset, en, reset
  D_Flip_Flop #(.trigger("falling")) d_ff_54 (
    .clk(and_14_out), .D(Entrada[4]), .Q(d_ff_54_q));  // open: Qn, preset, en, reset
  D_Flip_Flop #(.trigger("falling")) d_ff_55 (
    .clk(and_15_out), .D(Entrada[4]), .Q(d_ff_55_q));  // open: Qn, preset, en, reset
  D_Flip_Flop #(.trigger("falling")) d_ff_56 (
    .clk(and_16_out), .D(Entrada[4]), .Q(d_ff_56_q));  // open: Qn, preset, en, reset
  and and_65 (and_65_out, d_ff_49_q, and_1_out);
  and and_66 (and_66_out, d_ff_50_q, and_2_out);
  and and_67 (and_67_out, d_ff_51_q, and_3_out);
  and and_68 (and_68_out, d_ff_52_q, and_4_out);
  and and_69 (and_69_out, d_ff_53_q, and_5_out);
  and and_70 (and_70_out, d_ff_54_q, and_6_out);
  and and_71 (and_71_out, d_ff_55_q, and_7_out);
  and and_72 (and_72_out, d_ff_56_q, and_8_out);
  or or_7 (\Saída [4], and_72_out, and_71_out, and_70_out, and_69_out, and_68_out, and_67_out, and_66_out, and_65_out);
  D_Flip_Flop #(.trigger("falling")) d_ff_57 (
    .clk(and_9_out), .D(Entrada[3]), .Q(d_ff_57_q));  // open: Qn, preset, en, reset
  D_Flip_Flop #(.trigger("falling")) d_ff_58 (
    .clk(and_10_out), .D(Entrada[3]), .Q(d_ff_58_q));  // open: Qn, preset, en, reset
  D_Flip_Flop #(.trigger("falling")) d_ff_59 (
    .clk(and_11_out), .D(Entrada[3]), .Q(d_ff_59_q));  // open: Qn, preset, en, reset
  D_Flip_Flop #(.trigger("falling")) d_ff_60 (
    .clk(and_12_out), .D(Entrada[3]), .Q(d_ff_60_q));  // open: Qn, preset, en, reset
  D_Flip_Flop #(.trigger("falling")) d_ff_61 (
    .clk(and_13_out), .D(Entrada[3]), .Q(d_ff_61_q));  // open: Qn, preset, en, reset
  D_Flip_Flop #(.trigger("falling")) d_ff_62 (
    .clk(and_14_out), .D(Entrada[3]), .Q(d_ff_62_q));  // open: Qn, preset, en, reset
  D_Flip_Flop #(.trigger("falling")) d_ff_63 (
    .clk(and_15_out), .D(Entrada[3]), .Q(d_ff_63_q));  // open: Qn, preset, en, reset
  D_Flip_Flop #(.trigger("falling")) d_ff_64 (
    .clk(and_16_out), .D(Entrada[3]), .Q(d_ff_64_q));  // open: Qn, preset, en, reset
  and and_73 (and_73_out, d_ff_57_q, and_1_out);
  and and_74 (and_74_out, d_ff_58_q, and_2_out);
  and and_75 (and_75_out, d_ff_59_q, and_3_out);
  and and_76 (and_76_out, d_ff_60_q, and_4_out);
  and and_77 (and_77_out, d_ff_61_q, and_5_out);
  and and_78 (and_78_out, d_ff_62_q, and_6_out);
  and and_79 (and_79_out, d_ff_63_q, and_7_out);
  and and_80 (and_80_out, d_ff_64_q, and_8_out);
  or or_8 (\Saída [3], and_80_out, and_79_out, and_78_out, and_77_out, and_76_out, and_75_out, and_74_out, and_73_out);
  D_Flip_Flop #(.trigger("falling")) d_ff_65 (
    .clk(and_9_out), .D(Entrada[2]), .Q(d_ff_65_q));  // open: Qn, preset, en, reset
  and and_81 (and_81_out, d_ff_65_q, and_1_out);
  D_Flip_Flop #(.trigger("falling")) d_ff_66 (
    .clk(and_10_out), .D(Entrada[2]), .Q(d_ff_66_q));  // open: Qn, preset, en, reset
  and and_82 (and_82_out, d_ff_66_q, and_2_out);
  D_Flip_Flop #(.trigger("falling")) d_ff_67 (
    .clk(and_11_out), .D(Entrada[2]), .Q(d_ff_67_q));  // open: Qn, preset, en, reset
  and and_83 (and_83_out, d_ff_67_q, and_3_out);
  D_Flip_Flop #(.trigger("falling")) d_ff_68 (
    .clk(and_12_out), .D(Entrada[2]), .Q(d_ff_68_q));  // open: Qn, preset, en, reset
  and and_84 (and_84_out, d_ff_68_q, and_4_out);
  D_Flip_Flop #(.trigger("falling")) d_ff_69 (
    .clk(and_13_out), .D(Entrada[2]), .Q(d_ff_69_q));  // open: Qn, preset, en, reset
  and and_85 (and_85_out, d_ff_69_q, and_5_out);
  D_Flip_Flop #(.trigger("falling")) d_ff_70 (
    .clk(and_14_out), .D(Entrada[2]), .Q(d_ff_70_q));  // open: Qn, preset, en, reset
  and and_86 (and_86_out, d_ff_70_q, and_6_out);
  D_Flip_Flop #(.trigger("falling")) d_ff_71 (
    .clk(and_15_out), .D(Entrada[2]), .Q(d_ff_71_q));  // open: Qn, preset, en, reset
  and and_87 (and_87_out, d_ff_71_q, and_7_out);
  D_Flip_Flop #(.trigger("falling")) d_ff_72 (
    .clk(and_16_out), .D(Entrada[2]), .Q(d_ff_72_q));  // open: Qn, preset, en, reset
  and and_88 (and_88_out, d_ff_72_q, and_8_out);
  or or_9 (\Saída [2], and_88_out, and_87_out, and_86_out, and_85_out, and_84_out, and_83_out, and_82_out, and_81_out);
  D_Flip_Flop #(.trigger("falling")) d_ff_73 (
    .clk(and_9_out), .D(Entrada[1]), .Q(d_ff_73_q));  // open: Qn, preset, en, reset
  and and_89 (and_89_out, d_ff_73_q, and_1_out);
  D_Flip_Flop #(.trigger("falling")) d_ff_74 (
    .clk(and_10_out), .D(Entrada[1]), .Q(d_ff_74_q));  // open: Qn, preset, en, reset
  and and_90 (and_90_out, d_ff_74_q, and_2_out);
  D_Flip_Flop #(.trigger("falling")) d_ff_75 (
    .clk(and_11_out), .D(Entrada[1]), .Q(d_ff_75_q));  // open: Qn, preset, en, reset
  and and_91 (and_91_out, d_ff_75_q, and_3_out);
  D_Flip_Flop #(.trigger("falling")) d_ff_76 (
    .clk(and_12_out), .D(Entrada[1]), .Q(d_ff_76_q));  // open: Qn, preset, en, reset
  and and_92 (and_92_out, d_ff_76_q, and_4_out);
  D_Flip_Flop #(.trigger("falling")) d_ff_77 (
    .clk(and_13_out), .D(Entrada[1]), .Q(d_ff_77_q));  // open: Qn, preset, en, reset
  and and_93 (and_93_out, d_ff_77_q, and_5_out);
  D_Flip_Flop #(.trigger("falling")) d_ff_78 (
    .clk(and_14_out), .D(Entrada[1]), .Q(d_ff_78_q));  // open: Qn, preset, en, reset
  and and_94 (and_94_out, d_ff_78_q, and_6_out);
  D_Flip_Flop #(.trigger("falling")) d_ff_79 (
    .clk(and_15_out), .D(Entrada[1]), .Q(d_ff_79_q));  // open: Qn, preset, en, reset
  and and_95 (and_95_out, d_ff_79_q, and_7_out);
  D_Flip_Flop #(.trigger("falling")) d_ff_80 (
    .clk(and_16_out), .D(Entrada[1]), .Q(d_ff_80_q));  // open: Qn, preset, en, reset
  and and_96 (and_96_out, d_ff_80_q, and_8_out);
  or or_10 (\Saída [1], and_96_out, and_95_out, and_94_out, and_93_out, and_92_out, and_91_out, and_90_out, and_89_out);
  D_Flip_Flop #(.trigger("falling")) d_ff_81 (
    .clk(and_9_out), .D(Entrada[0]), .Q(d_ff_81_q));  // open: Qn, preset, en, reset
  D_Flip_Flop #(.trigger("falling")) d_ff_82 (
    .clk(and_10_out), .D(Entrada[0]), .Q(d_ff_82_q));  // open: Qn, preset, en, reset
  D_Flip_Flop #(.trigger("falling")) d_ff_83 (
    .clk(and_11_out), .D(Entrada[0]), .Q(d_ff_83_q));  // open: Qn, preset, en, reset
  D_Flip_Flop #(.trigger("falling")) d_ff_84 (
    .clk(and_12_out), .D(Entrada[0]), .Q(d_ff_84_q));  // open: Qn, preset, en, reset
  D_Flip_Flop #(.trigger("falling")) d_ff_85 (
    .clk(and_13_out), .D(Entrada[0]), .Q(d_ff_85_q));  // open: Qn, preset, en, reset
  D_Flip_Flop #(.trigger("falling")) d_ff_86 (
    .clk(and_14_out), .D(Entrada[0]), .Q(d_ff_86_q));  // open: Qn, preset, en, reset
  D_Flip_Flop #(.trigger("falling")) d_ff_87 (
    .clk(and_15_out), .D(Entrada[0]), .Q(d_ff_87_q));  // open: Qn, preset, en, reset
  D_Flip_Flop #(.trigger("falling")) d_ff_88 (
    .clk(and_16_out), .D(Entrada[0]), .Q(d_ff_88_q));  // open: Qn, preset, en, reset
  and and_97 (and_97_out, d_ff_81_q, and_1_out);
  and and_98 (and_98_out, d_ff_82_q, and_2_out);
  and and_99 (and_99_out, d_ff_83_q, and_3_out);
  and and_100 (and_100_out, d_ff_84_q, and_4_out);
  and and_101 (and_101_out, d_ff_85_q, and_5_out);
  and and_102 (and_102_out, d_ff_86_q, and_6_out);
  and and_103 (and_103_out, d_ff_87_q, and_7_out);
  and and_104 (and_104_out, d_ff_88_q, and_8_out);
  or or_11 (\Saída [0], and_104_out, and_103_out, and_102_out, and_101_out, and_100_out, and_99_out, and_98_out, and_97_out);
endmodule

module contador (
  input  Clock,
  output [2:0] \Saída 
);

  T_Flip_Flop #(.trigger("falling")) t_ff_1 (.clk(Clock), .T(1'b1), .Q(\Saída [0]));  // open: Qn, preset, reset, en
  T_Flip_Flop #(.trigger("falling")) t_ff_2 (
    .clk(\Saída [0]), .T(1'b1), .Q(\Saída [1]));  // open: Qn, preset, reset, en
  T_Flip_Flop #(.trigger("falling")) t_ff_3 (
    .clk(\Saída [1]), .T(1'b1), .Q(\Saída [2]));  // open: Qn, preset, reset, en
endmodule

module comp (
  input  [10:0] in_1,
  input  in_2
);

  wire clock_1_out;
  wire [2:0] \contador_1_saída ;
  wire [7:0] divider_1_out, divider_1_rem, divider_2_out, divider_2_rem, main_1_output,
       \registrador8bits_1_saída ;
  wire [10:0] \memoria11x8_1_saída ;

  Clock clock_1 (.out(clock_1_out));
  contador contador_1 (.Clock(clock_1_out), .\Saída (\contador_1_saída ));
  memoria11x8 memoria11x8_1 (
    .Entrada(in_1), .\Endereço (\contador_1_saída ), .Leitura_Escrita(in_2), .\Saída (\memoria11x8_1_saída ));
  // Probe on \memoria11x8_1_saída [10:8]
  main main_1 (
    .a(\memoria11x8_1_saída [7:0]), .b(\registrador8bits_1_saída ), .fs(\memoria11x8_1_saída [10:8]),
    .\output (main_1_output));  // open: cout_sub, cout_sum, sub, div, resto, mult
  // Probe on \memoria11x8_1_saída [7:0]
  registrador8bits registrador8bits_1 (
    .Entrada(main_1_output), .Leitura_escrita(clock_1_out), .\Saída (\registrador8bits_1_saída ));
  Divider divider_1 (
    .a(\registrador8bits_1_saída ), .b(8'h64), .out({{4{divider_1_out[7]}}, divider_1_out[3:0]}),
    .rem(divider_1_rem));  // open: upper
  Hex_Digit_Display hex_digit_display_1 (.value(divider_1_out[3:0]));  // open: dp
  Divider divider_2 (
    .a(divider_1_rem), .b(8'ha), .out({{4{divider_2_out[7]}}, divider_2_out[3:0]}),
    .rem({{4{divider_2_rem[7]}}, divider_2_rem[3:0]}));  // open: upper
  Hex_Digit_Display hex_digit_display_2 (.value(divider_2_out[3:0]));  // open: dp
  Hex_Digit_Display hex_digit_display_3 (.value(divider_2_rem[3:0]));  // open: dp
endmodule

module registrador8bits (
  input  [7:0] Entrada,
  input  Leitura_escrita,
  output [7:0] \Saída 
);

  D_Flip_Flop d_ff_1 (.clk(Leitura_escrita), .D(Entrada[7]), .Q(\Saída [7]));  // open: Qn, preset, en, reset
  D_Flip_Flop d_ff_2 (.clk(Leitura_escrita), .D(Entrada[6]), .Q(\Saída [6]));  // open: Qn, preset, en, reset
  D_Flip_Flop d_ff_3 (.clk(Leitura_escrita), .D(Entrada[5]), .Q(\Saída [5]));  // open: Qn, preset, en, reset
  D_Flip_Flop d_ff_4 (.clk(Leitura_escrita), .D(Entrada[4]), .Q(\Saída [4]));  // open: Qn, preset, en, reset
  D_Flip_Flop d_ff_5 (.clk(Leitura_escrita), .D(Entrada[3]), .Q(\Saída [3]));  // open: Qn, preset, en, reset
  D_Flip_Flop d_ff_6 (.clk(Leitura_escrita), .D(Entrada[2]), .Q(\Saída [2]));  // open: Qn, preset, en, reset
  D_Flip_Flop d_ff_7 (.clk(Leitura_escrita), .D(Entrada[1]), .Q(\Saída [1]));  // open: Qn, preset, en, reset
  D_Flip_Flop d_ff_8 (.clk(Leitura_escrita), .D(Entrada[0]), .Q(\Saída [0]));  // open: Qn, preset, en, reset
endmodule
